// Digital circuit DigLo66_Quiz1__01.dig as structural Verilog
module DigLo66_Quiz1__01 (
  input  [3:0] in,
  output out
);

  wire and_1_out, and_2_out, and_3_out, and_4_out, not_1_out, not_2_out, not_3_out, not_4_out, not_5_out,
       not_6_out;

  and and_1 (and_1_out, in[0], not_1_out, not_2_out);
  not not_1 (not_1_out, in[2]);
  not not_2 (not_2_out, in[3]);
  and and_2 (and_2_out, not_3_out, in[2], not_4_out);
  not not_3 (not_3_out, in[1]);
  not not_4 (not_4_out, in[3]);
  and and_3 (and_3_out, in[0], not_5_out, in[3]);
  not not_5 (not_5_out, in[1]);
  and and_4 (and_4_out, not_6_out, in[1], in[3]);
  not not_6 (not_6_out, in[0]);
  or or_1 (out, and_1_out, and_2_out, and_3_out, and_4_out);

  // Other names for the same wires on the sheet: a = in[0]; b = in[1]; c = in[2]; d = in[3]
endmodule
