// Digital circuit DigLo66_Quiz1__02.dig as structural Verilog
module DigLo66_Quiz1__02 (
  input  [2:0] in0,
  input  [2:0] in1,
  input  addsubtract,
  output [2:0] out
);

  wire [1:0] num0, num1;
  wire [2:0] add_3_s, sub_1_s;

  Add #(.Bits(1)) add_1 (.a(in0[0]), .b(in0[1]), .c_i(in0[2]), .s(num0[0]), .c_o(num0[1]));
  Add #(.Bits(1)) add_2 (.a(in1[0]), .b(in1[1]), .c_i(in1[2]), .s(num1[0]), .c_o(num1[1]));
  Add #(.Bits(3)) add_3 (.a({1'b0, num0}), .b({1'b0, num1}), .c_i(1'b0), .s(add_3_s));  // open: c_o
  Sub #(.Bits(3)) sub_1 (.a({1'b0, num0}), .b({1'b0, num1}), .c_i(1'b0), .s(sub_1_s));  // open: c_o
  Multiplexer #(.Bits(3)) multiplexer_1 (.sel(addsubtract), .in_0(add_3_s), .in_1(sub_1_s), .out(out));
endmodule
