// Digital circuit DigLo66_Quiz2_01.dig as structural Verilog
module DigLo66_Quiz2_01 (
  input  reset,
  input  clk,
  output C,
  output B,
  output A
);

  wire a_t, and_1_out, and_2_out, and_3_out, and_4_out, and_5_out, and_6_out, and_7_out, and_8_out,
       and_9_out, b_t, c_t, or_1_out, or_2_out, or_3_out, reset_t;

  not not_1 (reset_t, reset);
  and and_1 (and_1_out, B, a_t);
  and and_2 (and_2_out, C, A);
  and and_3 (and_3_out, c_t, A);
  and and_4 (and_4_out, B, a_t);
  and and_5 (and_5_out, c_t, b_t);
  and and_6 (and_6_out, C, B);
  or or_1 (or_1_out, and_1_out, and_2_out);
  or or_2 (or_2_out, and_3_out, and_4_out);
  or or_3 (or_3_out, and_5_out, and_6_out);
  and and_7 (and_7_out, or_1_out, reset_t);
  and and_8 (and_8_out, or_2_out, reset_t);
  and and_9 (and_9_out, or_3_out, reset_t);
  D_FF d_ff_1 (.D(and_7_out), .C(clk), .Q(C));  // open: nQ
  D_FF d_ff_2 (.D(and_8_out), .C(clk), .Q(B));  // open: nQ
  D_FF d_ff_3 (.D(and_9_out), .C(clk), .Q(A));  // open: nQ
  not not_2 (c_t, C);
  not not_3 (b_t, B);
  not not_4 (a_t, A);
endmodule
