// Digital circuit DigLo66_Quiz2_02.dig as structural Verilog
module DigLo66_Quiz2_02 (
  input  [15:0] A,
  input  \input ,
  input  clk,
  output [7:0] sqrt,
  output busy
);

  wire _255, and_1_out, cal, equal, less, more, not_1_out, not_2_out, or_1_out;
  wire [7:0] multiplexer_1_out, x_plus_1;
  wire [15:0] x_plus_1__2;

  Add #(.Bits(8)) add_1 (.a(sqrt), .b(8'h1), .c_i(1'b0), .s(x_plus_1));  // open: c_o
  or or_1 (or_1_out, \input , busy);
  Multiplexer #(.Bits(8)) multiplexer_1 (.sel(more), .in_0(x_plus_1), .in_1(sqrt), .out(multiplexer_1_out));
  Mul #(.Bits(8)) mul_1 (.a(x_plus_1), .b(x_plus_1), .mul(x_plus_1__2));
  Register #(.Bits(8)) register_1 (.D(multiplexer_1_out), .C(clk), .en(busy), .Q(sqrt));
  D_FF d_ff_1 (.D(or_1_out), .C(clk), .Q(cal));  // open: nQ
  Comparator #(.Bits(16)) comparator_1 (.a(x_plus_1__2), .b(A), .gt(more), .eq(equal), .lt(less));
  not not_1 (not_1_out, more);
  not not_2 (not_2_out, _255);
  and and_1 (and_1_out, not_1_out, cal, not_2_out);
  Comparator #(.Bits(8)) comparator_2 (.a(sqrt), .b({8{1'b1}}), .eq(_255));  // open: gt, lt
  D_FF d_ff_2 (.D(and_1_out), .C(clk), .Q(busy));  // open: nQ

  // Other names for the same wires on the sheet: in = \input ; x[7:0] = sqrt
endmodule
