// Digital circuit DigLo66_Quiz2_03.dig as structural Verilog
module DigLo66_Quiz2_03 (
  input  [15:0] A,
  input  \input ,
  input  clk,
  input  reset,
  output [15:0] mean,
  output busy
);

  wire and_1_out, and_2_out, and_4_out, and_5_out, d_ff_1_q, en, in_once, in_reset, or_1_out;
  wire [15:0] multiplexer_4_out;
  wire [31:0] cnt, cnt_plus_1, mean_raw, multiplexer_1_out, multiplexer_2_out, multiplexer_3_out, sum,
       sum_plus_a;

  D_FF d_ff_1 (.D(\input ), .C(clk), .Q(d_ff_1_q));  // open: nQ
  and and_1 (and_1_out, ~d_ff_1_q, \input );  // And
  Multiplexer #(.Bits(32)) multiplexer_1 (.sel(reset), .in_0(sum_plus_a), .in_1({32{1'b0}}), .out(multiplexer_1_out));
  Multiplexer #(.Bits(32)) multiplexer_2 (
    .sel(in_once), .in_0({32{1'b0}}), .in_1({{16{1'b0}}, A}), .out(multiplexer_2_out));
  and and_2 (and_2_out, ~busy, and_1_out);  // And
  Register #(.Bits(32)) register_1 (.D(multiplexer_1_out), .C(clk), .en(in_reset), .Q(sum));
  Add #(.Bits(32)) add_1 (.a(sum), .b(multiplexer_2_out), .c_i(1'b0), .s(sum_plus_a));  // open: c_o
  and and_3 (in_once, and_2_out, ~reset);  // And
  Add #(.Bits(32)) add_2 (.a(cnt), .b(32'h1), .c_i(1'b0), .s(cnt_plus_1));  // open: c_o
  or or_1 (or_1_out, busy, in_once);
  Div #(.Bits(32)) div_1 (.a(sum_plus_a), .b(cnt), .q(mean_raw));  // open: r
  and and_4 (and_4_out, ~busy, or_1_out);  // And
  Multiplexer #(.Bits(32)) multiplexer_3 (.sel(reset), .in_0(cnt_plus_1), .in_1({32{1'b0}}), .out(multiplexer_3_out));
  Multiplexer #(.Bits(16)) multiplexer_4 (
    .sel(reset), .in_0(mean_raw[15:0]), .in_1({16{1'b0}}), .out(multiplexer_4_out));
  and and_5 (and_5_out, and_4_out, ~reset);  // And
  Register #(.Bits(32)) register_2 (.D(multiplexer_3_out), .C(clk), .en(in_reset), .Q(cnt));
  D_FF d_ff_2 (.D(and_5_out), .C(clk), .Q(busy));  // open: nQ
  Register #(.Bits(16)) register_3 (.D(multiplexer_4_out), .C(clk), .en(en), .Q(mean));
  or or_2 (in_reset, reset, in_once);
  or or_3 (en, in_reset, busy);

  // Other names for the same wires on the sheet: in = \input 
endmodule
