// Digital circuit DigLo67_Exam1_02.dig as structural Verilog
module DigLo67_Exam1_02 (
  input  X0,
  input  X1,
  input  Y0,
  input  Y1,
  output [4:0] Z
);

  wire and_2_out, and_3_out, and_5_out, and_6_out, and_7_out, not_1_out, not_2_out, not_3_out;

  not not_1 (not_1_out, X0);
  not not_2 (not_2_out, Y1);
  not not_3 (not_3_out, Y0);
  and and_1 (Z[4], X1, X0, Y1, Y0);
  and and_2 (and_2_out, X1, Y1, Y0);
  and and_3 (and_3_out, X1, X0, Y1);
  and and_4 (Z[2], X1, not_1_out, Y1, not_3_out);
  and and_5 (and_5_out, X1, not_2_out, Y0);
  and and_6 (and_6_out, X1, X0, Y0);
  and and_7 (and_7_out, not_2_out, not_3_out);
  or or_1 (Z[3], and_2_out, and_3_out);
  or or_2 (Z[1], and_5_out, and_6_out);
  or or_3 (Z[0], X0, and_7_out);

  // Other names for the same wires on the sheet: _0 = Z[0]; _1 = Z[1]; _2 = Z[2]; _3 = Z[3]; _4 = Z[4]
endmodule
