// Digital circuit DigLo67_Exam2_01.dig as structural Verilog
module DigLo67_Exam2_01 (
  input  reset,
  input  clock,
  input  load,
  input  Z,
  input  Y,
  input  X,
  output A,
  output B,
  output C
);

  wire a_t, and_1_out, and_2_out, and_3_out, and_4_out, and_5_out, and_6_out, and_7_out, and_8_out, b_t, c_t,
       multiplexer_1_out, multiplexer_2_out, multiplexer_3_out, or_1_out, or_2_out, or_3_out, reset_t;

  not not_1 (reset_t, reset);
  and and_1 (and_1_out, b_t, C);
  and and_2 (and_2_out, a_t, C);
  and and_3 (and_3_out, A, B, c_t);
  and and_4 (and_4_out, A, b_t);
  and and_5 (and_5_out, A, C);
  or or_1 (or_1_out, and_1_out, and_2_out, and_3_out);
  or or_2 (or_2_out, and_4_out, c_t);
  or or_3 (or_3_out, and_5_out, B);
  Multiplexer multiplexer_1 (.sel(load), .in_0(or_1_out), .in_1(X), .out(multiplexer_1_out));
  Multiplexer multiplexer_2 (.sel(load), .in_0(or_2_out), .in_1(Y), .out(multiplexer_2_out));
  Multiplexer multiplexer_3 (.sel(load), .in_0(or_3_out), .in_1(Z), .out(multiplexer_3_out));
  and and_6 (and_6_out, multiplexer_1_out, reset_t);
  and and_7 (and_7_out, multiplexer_2_out, reset_t);
  and and_8 (and_8_out, multiplexer_3_out, reset_t);
  D_FF d_ff_1 (.D(and_6_out), .C(clock), .Q(A));  // open: nQ
  D_FF d_ff_2 (.D(and_7_out), .C(clock), .Q(B));  // open: nQ
  D_FF d_ff_3 (.D(and_8_out), .C(clock), .Q(C));  // open: nQ
  not not_2 (a_t, A);
  not not_3 (b_t, B);
  not not_4 (c_t, C);

  // Other names for the same wires on the sheet: clk = clock
endmodule
