// Digital circuit DigLo67_Exam2_02.dig as structural Verilog
module DigLo67_Exam2_02 (
  input  reset,
  input  [15:0] P,
  input  start,
  input  clock,
  output [15:0] W,
  output [15:0] H,
  output [31:0] A,
  output busy
);

  wire and_1_out, d_ff_1_q, multiplexer_1_out, not_1_out, not_2_out, run;
  wire [15:0] multiplexer_2_out, multiplexer_3_out, p_2, x, y;
  wire [31:0] multiplexer_4_out, x_y;

  Div #(.Bits(16)) div_1 (.a(P), .b(16'h4), .q(x));  // open: r
  Div #(.Bits(16)) div_2 (.a(P), .b(16'h2), .q(p_2));  // open: r
  Multiplexer multiplexer_1 (.sel(reset), .in_0(start), .in_1(1'b0), .out(multiplexer_1_out));
  Sub #(.Bits(16)) sub_1 (.a(p_2), .b(x), .c_i(1'b0), .s(y));  // open: c_o
  Mul #(.Bits(16)) mul_1 (.a(x), .b(y), .mul(x_y));
  D_FF d_ff_1 (.D(multiplexer_1_out), .C(clock), .Q(d_ff_1_q));  // open: nQ
  and and_1 (and_1_out, not_1_out, start);
  not not_1 (not_1_out, d_ff_1_q);
  Multiplexer #(.Bits(16)) multiplexer_2 (.sel(run), .in_0(H), .in_1(x), .out(multiplexer_2_out));
  Multiplexer #(.Bits(16)) multiplexer_3 (.sel(run), .in_0(W), .in_1(y), .out(multiplexer_3_out));
  Multiplexer #(.Bits(32)) multiplexer_4 (.sel(run), .in_0(A), .in_1(x_y), .out(multiplexer_4_out));
  not not_2 (not_2_out, busy);
  D_FF #(.Bits(16)) d_ff_2 (.D(multiplexer_2_out), .C(clock), .Q(H));  // open: nQ
  D_FF #(.Bits(16)) d_ff_3 (.D(multiplexer_3_out), .C(clock), .Q(W));  // open: nQ
  D_FF #(.Bits(32)) d_ff_4 (.D(multiplexer_4_out), .C(clock), .Q(A));  // open: nQ
  and and_2 (run, not_2_out, and_1_out);
  D_FF d_ff_5 (.D(run), .C(clock), .Q(busy));  // open: nQ

  // Other names for the same wires on the sheet: clk = clock
endmodule

/* Test case T01:
P start clock reset W H A busy 0 0 0 1 x x x x 0 0 1 1 x x x x 0 0 0 0 0 0 0 0 0 0 1 0 0 0 0 0 92 1 0 0 x x x x 92 1 1 0 x x x x 0 0 0 0 x x x x 0 0 1 0 x x x x 0 0 0 0 x x x x 0 0 1 0 x x x x 0 0 0 0 x x x x 0 0 1 0 x x x x 0 0 0 0 x x x x 0 0 1 0 x x x x 0 0 0 0 x x x x 0 0 1 0 x x x x 0 0 0 0 x x x x 0 0 1 0 x x x x 0 0 0 0 x x x x 0 0 1 0 x x x x 0 0 0 0 x x x x 0 0 1 0 x x x x 0 0 0 0 x x x x 0 0 1 0 x x x x 0 0 0 0 x x x x 0 0 1 0 x x x x 0 0 0 0 x x x x 0 0 1 0 x x x x 0 0 0 0 x x x x 0 0 1 0 x x x x 0 0 0 0 x x x x 0 0 1 0 x x x x 0 0 0 0 x x x x 0 0 1 0 x x x x 0 0 0 0 x x x x 0 0 1 0 x x x x 0 0 0 0 x x x x 0 0 1 0 x x x x 0 0 0 0 x x x x 0 0 1 0 x x x x 0 0 0 0 x x x x 0 0 1 0 x x x x 0 0 0 0 x x x x 0 0 1 0 x x x x 0 0 0 0 x x x x 0 0 1 0 x x x x 0 0 0 0 x x x x 0 0 1 0 x x x x 0 0 0 0 x x x x 0 0 1 0 x x x x 0 0 0 0 x x x x 0 0 1 0 x x x x 0 0 0 0 x x x x 0 0 1 0 x x x x 0 0 0 0 x x x x 0 0 1 0 x x x x 0 0 0 0 x x x x 0 0 1 0 x x x x 0 0 0 0 x x x x 0 0 1 0 x x x x 0 0 0 0 x x x x 0 0 1 0 x x x x 0 0 0 0 x x x x 0 0 1 0 x x x x 0 0 0 0 x x x x 0 0 1 0 x x x x 0 0 0 0 x x x x 0 0 1 0 x x x x 0 0 0 0 x x x x 0 0 1 0 x x x x 0 0 0 0 x x x x 0 0 1 0 x x x x 0 0 0 0 x x x x 0 0 1 0 x x x x 0 0 0 0 x x x x 0 0 1 0 x x x x 0 0 0 0 x x x x 0 0 1 0 x x x x 0 0 0 0 x x x x 0 0 1 0 x x x x 0 0 0 0 x x x x 0 0 1 0 x x x x 0 0 0 0 x x x x 0 0 1 0 x x x x 0 0 0 0 x x x x 0 0 1 0 x x x x 0 0 0 0 x x x x 0 0 1 0 x x x x 0 0 0 0 x x x x 0 0 1 0 x x x x 0 0 0 0 x x x x 0 0 1 0 x x x x 0 0 0 0 x x x x 0 0 1 0 x x x x 0 0 0 0 x x x x 0 0 1 0 x x x x 0 0 0 0 x x x x 0 0 1 0 x x x x 0 0 0 0 x x x x 0 0 1 0 x x x x 0 0 0 0 x x x x 0 0 1 0 x x x x 0 0 0 0 x x x x 0 0 1 0 x x x x 0 0 0 0 x x x x 0 0 1 0 x x x x 0 0 0 0 x x x x 0 0 1 0 x x x x 0 0 0 0 x x x x 0 0 1 0 x x x x 0 0 0 0 x x x x 0 0 1 0 x x x x 0 0 0 0 x x x x 0 0 1 0 x x x x 0 0 0 0 x x x x 0 0 1 0 x x x x 0 0 0 0 x x x x 0 0 1 0 x x x x 0 0 0 0 x x x x 0 0 1 0 x x x x 0 0 0 0 x x x x 0 0 1 0 x x x x 0 0 0 0 x x x x 0 0 1 0 x x x x 0 0 0 0 x x x x 0 0 1 0 x x x x 0 0 0 0 x x x x 0 0 1 0 x x x x 0 0 0 0 x x x x 0 0 1 0 x x x x 0 0 0 0 x x x x 0 0 1 0 x x x x 0 0 0 0 x x x x 0 0 1 0 x x x x 0 0 0 0 x x x x 0 0 1 0 x x x x 0 0 0 0 x x x x 0 0 1 0 x x x x 0 0 0 0 x x x x 0 0 1 0 x x x x 0 0 0 0 x x x x 0 0 1 0 x x x x 0 0 0 0 x x x x 0 0 1 0 x x x x 0 0 0 0 x x x x 0 0 1 0 x x x x 0 0 0 0 x x x x 0 0 1 0 x x x x 0 0 0 0 x x x x 0 0 1 0 x x x x 0 0 0 0 x x x x 0 0 1 0 x x x x 0 0 0 0 x x x x 0 0 1 0 x x x x 0 0 0 0 x x x x 0 0 1 0 x x x x 0 0 0 0 x x x x 0 0 1 0 x x x x 0 0 0 0 x x x x 0 0 1 0 x x x x 0 0 0 0 x x x x 0 0 1 0 x x x x 0 0 0 0 x x x x 0 0 1 0 x x x x 0 0 0 0 x x x x 0 0 1 0 x x x x 0 0 0 0 x x x x 0 0 1 0 x x x x 0 0 0 0 x x x x 0 0 1 0 x x x x 0 0 0 0 x x x x 0 0 1 0 x x x x 0 0 0 0 x x x x 0 0 1 0 x x x x 0 0 0 0 x x x x 0 0 1 0 x x x x 0 0 0 0 x x x x 0 0 1 0 x x x x 0 0 0 0 x x x x 0 0 1 0 x x x x 0 0 0 0 x x x x 0 0 1 0 x x x x 0 0 0 0 x x x x 0 0 1 0 x x x x 0 0 0 0 x x x x 0 0 1 0 x x x x 0 0 0 0 x x x x 0 0 1 0 x x x x 0 0 0 0 x x x x 0 0 1 0 x x x x 0 0 0 0 x x x x 0 0 1 0 x x x x 0 0 0 0 x x x x 0 0 1 0 x x x x 0 0 0 0 x x x x 0 0 1 0 x x x x 0 0 0 0 x x x x 0 0 1 0 x x x x 0 0 0 0 x x x x 0 0 1 0 x x x x 0 0 0 0 x x x x 0 0 1 0 x x x x 0 0 0 0 x x x x 0 0 1 0 x x x x 0 0 0 0 x x x x 0 0 1 0 x x x x 0 0 0 0 x x x x 0 0 1 0 x x x x 0 0 0 0 x x x x 0 0 1 0 x x x x 0 0 0 0 x x x x 0 0 1 0 x x x x 0 0 0 0 x x x x 0 0 1 0 x x x x 0 0 0 0 x x x x 0 0 1 0 x x x x 0 0 0 0 x x x x 0 0 1 0 x x x x 0 0 0 0 x x x x 0 0 1 0 x x x x 0 0 0 0 x x x x 0 0 1 0 x x x x 0 0 0 0 x x x x 0 0 1 0 x x x x 0 0 0 0 x x x x 0 0 1 0 x x x x 0 0 0 0 x x x x 0 0 1 0 x x x x 0 0 0 0 x x x x 0 0 1 0 x x x x 0 0 0 0 x x x x 0 0 1 0 x x x x 0 0 0 0 x x x x 0 0 1 0 x x x x 0 0 0 0 x x x x 0 0 1 0 x x x x 0 0 0 0 x x x x 0 0 1 0 x x x x 0 0 0 0 x x x x 0 0 1 0 x x x x 0 0 0 0 x x x x 0 0 1 0 x x x x 0 0 0 0 x x x x 0 0 1 0 x x x x 0 0 0 0 x x x x 0 0 1 0 x x x x 0 0 0 0 x x x x 0 0 1 0 x x x x
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*/
