// Digital circuit DigLo67_Exam2_03.dig as structural Verilog
module DigLo67_Exam2_03 (
  input  reset,
  input  [7:0] N,
  input  \new ,
  input  clock,
  output [7:0] num_inc,
  output [7:0] max,
  output busy
);

  wire and_1_out, and_2_out, and_4_out, and_5_out, d_ff_1_q, en, more, new_once, new_reset, or_2_out;
  wire [7:0] multiplexer_1_out, multiplexer_2_out, multiplexer_3_out, multiplexer_4_out, multiplexer_5_out,
       n_val, num_inc_plus_1;

  D_FF d_ff_1 (.D(\new ), .C(clock), .Q(d_ff_1_q));  // open: nQ
  and and_1 (and_1_out, ~d_ff_1_q, \new );  // And
  and and_2 (and_2_out, ~busy, and_1_out);  // And
  Multiplexer #(.Bits(8)) multiplexer_1 (.sel(reset), .in_0(N), .in_1({8{1'b0}}), .out(multiplexer_1_out));
  Comparator #(.Bits(8)) comparator_1 (.a(n_val), .b(max), .gt(more));  // open: eq, lt
  Register #(.Bits(8)) register_1 (.D(multiplexer_1_out), .C(clock), .en(new_reset), .Q(n_val));
  and and_3 (new_once, ~reset, and_2_out);  // And
  Multiplexer #(.Bits(8)) multiplexer_2 (.sel(more), .in_0({8{1'b0}}), .in_1(8'h1), .out(multiplexer_2_out));
  Add #(.Bits(8)) add_1 (.a(num_inc), .b(multiplexer_2_out), .c_i(1'b0), .s(num_inc_plus_1));  // open: c_o
  Multiplexer #(.Bits(8)) multiplexer_3 (.sel(more), .in_0(max), .in_1(n_val), .out(multiplexer_3_out));
  or or_1 (new_reset, new_once, reset);
  Multiplexer #(.Bits(8)) multiplexer_4 (
    .sel(reset), .in_0(multiplexer_3_out), .in_1({8{1'b0}}), .out(multiplexer_4_out));
  or or_2 (or_2_out, busy, new_once);
  or or_3 (en, busy, new_reset);
  and and_4 (and_4_out, ~busy, or_2_out);  // And
  Register #(.Bits(8)) register_2 (.D(multiplexer_4_out), .C(clock), .en(en), .Q(max));
  Multiplexer #(.Bits(8)) multiplexer_5 (.sel(reset), .in_0(num_inc_plus_1), .in_1({8{1'b0}}), .out(multiplexer_5_out));
  Register #(.Bits(8)) register_3 (.D(multiplexer_5_out), .C(clock), .en(en), .Q(num_inc));
  and and_5 (and_5_out, ~reset, and_4_out);  // And
  D_FF d_ff_2 (.D(and_5_out), .C(clock), .Q(busy));  // open: nQ

  // Other names for the same wires on the sheet: clk = clock
endmodule

/* Test case T06:
N new reset clock num_inc max busy 0 0 1 0 x x x 0 0 1 1 0 0 0 131 1 0 0 x x x 131 1 0 1 x x x 0 0 0 0 x x x 0 0 0 1 x x x 0 0 0 0 x x x 0 0 0 1 x x x 0 0 0 0 x x x 0 0 0 1 x x x 0 0 0 0 x x x 0 0 0 1 x x x 0 0 0 0 x x x 0 0 0 1 x x x 0 0 0 0 x x x 0 0 0 1 x x x 0 0 0 0 x x x 0 0 0 1 x x x 0 0 0 0 x x x 0 0 0 1 x x x 0 0 0 0 x x x 0 0 0 1 x x x 0 0 0 0 x x x 0 0 0 1 x x x 0 0 0 0 x x x 0 0 0 1 x x x 0 0 0 0 x x x 0 0 0 1 x x x 0 0 0 0 x x x 0 0 0 1 x x x 0 0 0 0 x x x 0 0 0 1 x x x 0 0 0 0 x x x 0 0 0 1 x x x 0 0 0 0 x x x 0 0 0 1 x x x 0 0 0 0 x x x 0 0 0 1 x x x 0 0 0 0 x x x 0 0 0 1 x x x 0 0 0 0 x x x 0 0 0 1 x x x 0 0 0 0 x x x 0 0 0 1 x x x 0 0 0 0 x x x 0 0 0 1 x x x 0 0 0 0 x x x 0 0 0 1 x x x 0 0 0 0 x x x 0 0 0 1 x x x 0 0 0 0 x x x 0 0 0 1 x x x 0 0 0 0 x x x 0 0 0 1 x x x 0 0 0 0 x x x 0 0 0 1 x x x 0 0 0 0 x x x 0 0 0 1 x x x 0 0 0 0 x x x 0 0 0 1 x x x 0 0 0 0 x x x 0 0 0 1 x x x 0 0 0 0 x x x 0 0 0 1 x x x 0 0 0 0 1 131 0 0 0 0 1 1 131 0 130 1 0 0 x x x 130 1 0 1 x x x 0 0 0 0 x x x 0 0 0 1 x x x 0 0 0 0 x x x 0 0 0 1 x x x 0 0 0 0 x x x 0 0 0 1 x x x 0 0 0 0 x x x 0 0 0 1 x x x 0 0 0 0 x x x 0 0 0 1 x x x 0 0 0 0 x x x 0 0 0 1 x x x 0 0 0 0 x x x 0 0 0 1 x x x 0 0 0 0 x x x 0 0 0 1 x x x 0 0 0 0 x x x 0 0 0 1 x x x 0 0 0 0 x x x 0 0 0 1 x x x 0 0 0 0 x x x 0 0 0 1 x x x 0 0 0 0 x x x 0 0 0 1 x x x 0 0 0 0 x x x 0 0 0 1 x x x 0 0 0 0 x x x 0 0 0 1 x x x 0 0 0 0 x x x 0 0 0 1 x x x 0 0 0 0 x x x 0 0 0 1 x x x 0 0 0 0 x x x 0 0 0 1 x x x 0 0 0 0 x x x 0 0 0 1 x x x 0 0 0 0 x x x 0 0 0 1 x x x 0 0 0 0 x x x 0 0 0 1 x x x 0 0 0 0 x x x 0 0 0 1 x x x 0 0 0 0 x x x 0 0 0 1 x x x 0 0 0 0 x x x 0 0 0 1 x x x 0 0 0 0 x x x 0 0 0 1 x x x 0 0 0 0 x x x 0 0 0 1 x x x 0 0 0 0 x x x 0 0 0 1 x x x 0 0 0 0 x x x 0 0 0 1 x x x 0 0 0 0 x x x 0 0 0 1 x x x 0 0 0 0 x x x 0 0 0 1 x x x 0 0 0 0 x x x 0 0 0 1 x x x 0 0 0 0 1 131 0 0 0 0 1 1 131 0 58 1 0 0 x x x 58 1 0 1 x x x 0 0 0 0 x x x 0 0 0 1 x x x 0 0 0 0 x x x 0 0 0 1 x x x 0 0 0 0 x x x 0 0 0 1 x x x 0 0 0 0 x x x 0 0 0 1 x x x 0 0 0 0 x x x 0 0 0 1 x x x 0 0 0 0 x x x 0 0 0 1 x x x 0 0 0 0 x x x 0 0 0 1 x x x 0 0 0 0 x x x 0 0 0 1 x x x 0 0 0 0 x x x 0 0 0 1 x x x 0 0 0 0 x x x 0 0 0 1 x x x 0 0 0 0 x x x 0 0 0 1 x x x 0 0 0 0 x x x 0 0 0 1 x x x 0 0 0 0 x x x 0 0 0 1 x x x 0 0 0 0 x x x 0 0 0 1 x x x 0 0 0 0 x x x 0 0 0 1 x x x 0 0 0 0 x x x 0 0 0 1 x x x 0 0 0 0 x x x 0 0 0 1 x x x 0 0 0 0 x x x 0 0 0 1 x x x 0 0 0 0 x x x 0 0 0 1 x x x 0 0 0 0 x x x 0 0 0 1 x x x 0 0 0 0 x x x 0 0 0 1 x x x 0 0 0 0 x x x 0 0 0 1 x x x 0 0 0 0 x x x 0 0 0 1 x x x 0 0 0 0 x x x 0 0 0 1 x x x 0 0 0 0 x x x 0 0 0 1 x x x 0 0 0 0 x x x 0 0 0 1 x x x 0 0 0 0 x x x 0 0 0 1 x x x 0 0 0 0 x x x 0 0 0 1 x x x 0 0 0 0 x x x 0 0 0 1 x x x 0 0 0 0 x x x 0 0 0 1 x x x 0 0 0 0 1 131 0 0 0 0 1 1 131 0 154 1 0 0 x x x 154 1 0 1 x x x 0 0 0 0 x x x 0 0 0 1 x x x 0 0 0 0 x x x 0 0 0 1 x x x 0 0 0 0 x x x 0 0 0 1 x x x 0 0 0 0 x x x 0 0 0 1 x x x 0 0 0 0 x x x 0 0 0 1 x x x 0 0 0 0 x x x 0 0 0 1 x x x 0 0 0 0 x x x 0 0 0 1 x x x 0 0 0 0 x x x 0 0 0 1 x x x 0 0 0 0 x x x 0 0 0 1 x x x 0 0 0 0 x x x 0 0 0 1 x x x 0 0 0 0 x x x 0 0 0 1 x x x 0 0 0 0 x x x 0 0 0 1 x x x 0 0 0 0 x x x 0 0 0 1 x x x 0 0 0 0 x x x 0 0 0 1 x x x 0 0 0 0 x x x 0 0 0 1 x x x 0 0 0 0 x x x 0 0 0 1 x x x 0 0 0 0 x x x 0 0 0 1 x x x 0 0 0 0 x x x 0 0 0 1 x x x 0 0 0 0 x x x 0 0 0 1 x x x 0 0 0 0 x x x 0 0 0 1 x x x 0 0 0 0 x x x 0 0 0 1 x x x 0 0 0 0 x x x 0 0 0 1 x x x 0 0 0 0 x x x 0 0 0 1 x x x 0 0 0 0 x x x 0 0 0 1 x x x 0 0 0 0 x x x 0 0 0 1 x x x 0 0 0 0 x x x 0 0 0 1 x x x 0 0 0 0 x x x 0 0 0 1 x x x 0 0 0 0 x x x 0 0 0 1 x x x 0 0 0 0 x x x 0 0 0 1 x x x 0 0 0 0 x x x 0 0 0 1 x x x 0 0 0 0 2 154 0 0 0 0 1 2 154 0 122 1 0 0 x x x 122 1 0 1 x x x 0 0 0 0 x x x 0 0 0 1 x x x 0 0 0 0 x x x 0 0 0 1 x x x 0 0 0 0 x x x 0 0 0 1 x x x 0 0 0 0 x x x 0 0 0 1 x x x 0 0 0 0 x x x 0 0 0 1 x x x 0 0 0 0 x x x 0 0 0 1 x x x 0 0 0 0 x x x 0 0 0 1 x x x 0 0 0 0 x x x 0 0 0 1 x x x 0 0 0 0 x x x 0 0 0 1 x x x 0 0 0 0 x x x 0 0 0 1 x x x 0 0 0 0 x x
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*/
