// Digital circuit DigLo68_Exam1_1.dig as structural Verilog
module DigLo68_Exam1_1 (
  input  X3,
  input  X2,
  input  X1,
  input  X0,
  output Y1,
  output [4:0] CheckGlitch
);

  wire and_1_out, and_2_out, and_3_out, and_4_out, and_5_out, and_6_out, x0_t, x1_t, x2_t, x3_t;

  not not_1 (x3_t, X3);
  not not_2 (x2_t, X2);
  not not_3 (x1_t, X1);
  not not_4 (x0_t, X0);
  and and_1 (and_1_out, X3, X2, x1_t);
  and and_2 (and_2_out, X3, X1, x0_t);
  and and_3 (and_3_out, X3, x2_t, X1);
  and and_4 (and_4_out, x2_t, X0);
  and and_5 (and_5_out, X3, X2, x0_t);
  and and_6 (and_6_out, X3, x1_t, X0);
  or or_1 (Y1, and_1_out, and_2_out, and_3_out, and_4_out, and_5_out, and_6_out);
  Counter #(.Bits(5)) counter_1 (.en(1'b1), .C(Y1), .clr(1'b0), .out(CheckGlitch));  // open: ovf

  // Other names for the same wires on the sheet: z = Y1

  // Notes on the sheet:
  //   Don't change anything inside this box
endmodule

/* Test case T1:
X3 X2 X1 X0 Y1 CheckGlitch 0 0 0 0 0 0 0 0 0 0 0 0 0 1 0 0 0 0 1 1 0 0 1 1 1 1 0 0 1 1 1 1 0 1 1 1 0 1 0 1 0 1 0 0 0 1 1 2 0 0 1 1 1 2
*/
