// Digital circuit DigLo68_Exam1_2.dig as structural Verilog
module DigLo68_Exam1_2 (
  input  X3,
  input  X2,
  input  X1,
  input  X0,
  output Z3,
  output Z2,
  output Z1,
  output Z0
);

  wire and_1_out, and_2_out, and_3_out, and_4_out, not_5_out, not_6_out, not_7_out, not_8_out, not_9_out,
       x_0, x_1, x_2, x_3;
  wire [3:0] r2, r3, r5;

  not not_1 (x_3, X3);
  not not_2 (x_2, X2);
  not not_3 (x_1, X1);
  Div #(.Bits(4)) div_1 (.a({X3, X2, X1, X0}), .b(4'b0010), .r(r2));  // open: q
  Div #(.Bits(4)) div_2 (.a({X3, X2, X1, X0}), .b(4'b0011), .r(r3));  // open: q
  Div #(.Bits(4)) div_3 (.a({X3, X2, X1, X0}), .b(4'b0101), .r(r5));  // open: q
  not not_4 (x_0, X0);
  nor nor_1 (Z2, r2[0], r2[1], r2[2], r2[3]);
  nor nor_2 (Z1, r3[0], r3[1], r3[2], r3[3]);
  nor nor_3 (Z0, r5[0], r5[1], r5[2], r5[3]);
  and and_1 (and_1_out, X0, X1, not_5_out);
  not not_5 (not_5_out, X3);
  and and_2 (and_2_out, X1, not_6_out, not_7_out);
  not not_6 (not_6_out, X2);
  not not_7 (not_7_out, X3);
  and and_3 (and_3_out, X0, not_8_out, X2);
  not not_8 (not_8_out, X1);
  and and_4 (and_4_out, X0, X1, not_9_out);
  not not_9 (not_9_out, X2);
  or or_1 (Z3, and_1_out, and_2_out, and_3_out, and_4_out);

  // Notes on the sheet:
  //   Z3: Is prime number?
  //   Z2: Is it divisible by 2?
  //   Z1: Is it divisible by 3?
  //   Z0: Is it divisible by 5?
  //   Don't change anything inside this box
endmodule

/* Test case T1:
X3 X2 X1 X0 Z3 Z2 Z1 Z0 0 0 0 0 0 1 1 1 0 1 1 1 1 0 0 0 1 0 1 0 0 1 0 1 
*/
