// Digital circuit DigLo68_Exam1_3.dig as structural Verilog
module DigLo68_Exam1_3 (
  input  SM,
  input  SN,
  input  TE,
  input  RA,
  input  AH,
  input  LI,
  input  MW,
  input  MF,
  output WP,
  output FD
);

  wire AH_t, and_1_out, and_2_out, LI_t, MF_t, MW_t, not_8_out, or_1_out, or_2_out, RA_t, SM_t, SN_t, TE_t;

  not not_1 (SM_t, SM);
  not not_2 (SN_t, SN);
  and and_1 (and_1_out, SN, SM_t, RA_t);
  not not_3 (TE_t, TE);
  or or_1 (or_1_out, TE, AH);
  not not_4 (RA_t, RA);
  not not_5 (AH_t, AH);
  and and_2 (and_2_out, SM, RA_t, LI, or_1_out);
  or or_2 (or_2_out, and_1_out, MF);
  not not_6 (LI_t, LI);
  not not_7 (MW_t, MW);
  or or_3 (WP, and_2_out, MW);
  and and_3 (FD, or_2_out, not_8_out);
  not not_8 (not_8_out, WP);
  not not_9 (MF_t, MF);

  // Notes on the sheet:
  //   WP: WP – Water Pump (1=เปิดรดน้ำ)
  //   FD: FD – Fertilizer Dispenser (1=เปิดใส่ปุ๋ย)
  //   SM: SM – Soil Moisture (ดินแห้ง=1, ดินชื้น=0)
  //   SN: SN – Soil Nutrient (ธาตุอาหารต่ำ=1, เพียงพอ=0)
  //   TE: TE – Temperature (อุณหภูมิสูงเกิน 35°C =1)
  //   RA: RA – Rain (มีฝนตก=1, ไม่มีฝน=0)
  //   AH: AH – Air Humidity (ความชื้นอากาศต่ำ=1)
  //   LI: LI – Light (แสงแดดแรง=1)
  //   MW: MW – Manual Water (ผู้ใช้สั่ง “รดน้ำ” =1)
  //   MF: MF – Manual Fertilize (ผู้ใช้สั่ง “ใส่ปุ๋ย” =1)
  //   Don't change anything inside this box
endmodule

/* Test case T1:
SM SN TE RA AH LI MW MF WP FD 0 0 0 0 0 0 0 0 0 0 1 0 1 0 0 1 0 0 1 0 1 0 1 0 0 0 0 0 0 0 0 0 0 0 0 0 1 0 1 0 0 0 0 0 0 0 0 1 0 1 
*/
