// Digital circuit DigLo68_Exam2_1.dig as structural Verilog
module DigLo68_Exam2_1 (
  input  reset,
  input  X,
  input  Y,
  input  Z,
  input  load,
  input  clock,
  output A,
  output B,
  output C
);

  wire a_t, and_1_out, and_2_out, and_3_out, and_4_out, and_5_out, and_6_out, and_7_out, b_t, c_t,
       multiplexer_1_out, multiplexer_2_out, multiplexer_3_out, multiplexer_4_out, or_1_out, or_2_out,
       or_3_out, reset_t;

  not not_1 (reset_t, reset);
  and and_1 (and_1_out, b_t, C);
  and and_2 (and_2_out, A, C);
  and and_3 (and_3_out, a_t, c_t);
  and and_4 (and_4_out, a_t, b_t);
  and and_5 (and_5_out, A, B, c_t);
  or or_1 (or_1_out, and_1_out, and_2_out, and_3_out);
  or or_2 (or_2_out, b_t, c_t);
  or or_3 (or_3_out, and_4_out, and_5_out);
  Multiplexer multiplexer_1 (.sel(load), .in_0(or_1_out), .in_1(X), .out(multiplexer_1_out));
  Multiplexer multiplexer_2 (.sel(load), .in_0(or_3_out), .in_1(Z), .out(multiplexer_2_out));
  and and_6 (and_6_out, multiplexer_1_out, reset_t);
  Multiplexer multiplexer_3 (.sel(load), .in_0(or_2_out), .in_1(Y), .out(multiplexer_3_out));
  and and_7 (and_7_out, multiplexer_2_out, reset_t);
  Multiplexer multiplexer_4 (.sel(reset_t), .in_0(1'b1), .in_1(multiplexer_3_out), .out(multiplexer_4_out));
  D_FF d_ff_1 (.D(and_6_out), .C(clock), .Q(A));  // open: nQ
  D_FF d_ff_2 (.D(multiplexer_4_out), .C(clock), .Q(B));  // open: nQ
  D_FF d_ff_3 (.D(and_7_out), .C(clock), .Q(C));  // open: nQ
  not not_2 (a_t, A);
  not not_3 (b_t, B);
  not not_4 (c_t, C);

  // Other names for the same wires on the sheet: clk = clock
endmodule

/* Test case T01:
X Y Z reset load clock A B C 
0 0 0 1 0 0 x x x 
0 0 0 1 0 1 0 1 0 
1 1 0 0 1 0 0 1 0 
1 1 0 0 1 1 1 1 0 
0 0 0 0 0 0 1 1 0 
0 0 0 0 0 1 0 1 1 
0 0 0 0 0 0 0 1 1 
0 0 0 0 0 1 0 0 0 
0 0 0 0 0 0 0 0 0 
0 0 0 0 0 1 1 1 1 
0 0 0 0 0 0 1 1 1 
0 0 0 0 0 1 1 0 0 
0 0 0 0 0 0 1 0 0 
0 0 0 0 0 1 0 1 0 
0 0 0 0 0 0 0 1 0 
0 0 0 0 0 1 1 1 0 
0 0 0 0 0 0 1 1 0 
0 0 0 0 0 1 0 1 1 
0 0 0 0 0 0 0 1 1 
0 0 0 0 0 1 0 0 0 
0 0 0 0 0 0 0 0 0 
*/
