// Digital circuit DigLo68_Exam2_2.dig as structural Verilog
module DigLo68_Exam2_2 (
  input  reset,
  input  [7:0] M,
  input  start,
  input  clock,
  input  [7:0] N,
  output [15:0] Z,
  output busy
);

  wire and_1_out, and_2_out, and_5_out, and_6_out, d_ff_1_q, en, loop, more, or_1_out, r, start_once;
  wire [7:0] m_plus_1, m_val, multiplexer_1_out, multiplexer_3_out, n_val;
  wire [7:1] div_1_r;
  wire [15:0] multiplexer_2_out, multiplexer_4_out, multiplexer_5_out, z_plus_m;

  D_FF d_ff_1 (.D(start), .C(clock), .Q(d_ff_1_q));  // open: nQ
  and and_1 (and_1_out, ~d_ff_1_q, start);  // And
  Register #(.Bits(8)) register_1 (.D(N), .C(clock), .en(start_once), .Q(n_val));
  Div #(.Bits(8)) div_1 (.a(m_val), .b(8'h2), .r({div_1_r, r}));  // open: q
  and and_2 (and_2_out, and_1_out, ~busy);  // And
  Multiplexer #(.Bits(8)) multiplexer_1 (.sel(start_once), .in_0(m_plus_1), .in_1(M), .out(multiplexer_1_out));
  Multiplexer #(.Bits(16)) multiplexer_2 (
    .sel(r), .in_0({{8{1'b0}}, m_val}), .in_1({16{1'b0}}), .out(multiplexer_2_out));
  and and_3 (start_once, ~reset, and_2_out);  // And
  Multiplexer #(.Bits(8)) multiplexer_3 (
    .sel(reset), .in_0(multiplexer_1_out), .in_1({8{1'b0}}), .out(multiplexer_3_out));
  Add #(.Bits(16)) add_1 (.a(multiplexer_2_out), .b(Z), .c_i(1'b0), .s(z_plus_m));  // open: c_o
  Register #(.Bits(8)) register_2 (.D(multiplexer_3_out), .C(clock), .en(en), .Q(m_val));
  Add #(.Bits(8)) add_2 (.a(m_val), .b(8'h1), .c_i(1'b0), .s(m_plus_1));  // open: c_o
  and and_4 (loop, ~more, busy);  // And
  Comparator #(.Bits(8)) comparator_1 (.a(m_val), .b(n_val), .gt(more));  // open: eq, lt
  or or_1 (or_1_out, loop, start_once);
  and and_5 (and_5_out, ~busy, start_once);  // And
  Multiplexer #(.Bits(16)) multiplexer_4 (.sel(and_5_out), .in_0(z_plus_m), .in_1({16{1'b0}}), .out(multiplexer_4_out));
  and and_6 (and_6_out, or_1_out, ~reset);  // And
  or or_2 (en, loop, start_once, reset);
  Multiplexer #(.Bits(16)) multiplexer_5 (
    .sel(reset), .in_0(multiplexer_4_out), .in_1({16{1'b0}}), .out(multiplexer_5_out));
  D_FF d_ff_2 (.D(and_6_out), .C(clock), .Q(busy));  // open: nQ
  Register #(.Bits(16)) register_3 (.D(multiplexer_5_out), .C(clock), .en(en), .Q(Z));

  // Other names for the same wires on the sheet: clk = clock
endmodule

/* Test case T01:
M   N  start  clock  reset   Z  busy
0   0      0      0      1   x     x
0   0      0      1      1   x     0
0   0      0      0      1   x     0
0   0      0      1      1   x     0
1  10      1      0      0   x     0
1  10      1      1      0   x     1
0   0      0      0      0   x     1
0   0      0      1      0   x     1
0   0      0      0      0   x     1
0   0      0      1      0   x     1
0   0      0      0      0   x     1
0   0      0      1      0   x     x
0   0      0      0      0   x     x
0   0      0      1      0   x     x
0   0      0      0      0   x     x
0   0      0      1      0   x     x
0   0      0      0      0   x     x
0   0      0      1      0   x     x
0   0      0      0      0   x     x
0   0      0      1      0   x     x
0   0      0      0      0   x     x
0   0      0      1      0   x     x
0   0      0      0      0   x     x
0   0      0      1      0   x     x
0   0      0      0      0   x     x
0   0      0      1      0   x     x
0   0      0      0      0   x     x
0   0      0      1      0   x     x
0   0      0      0      0   x     x
0   0      0      1      0   x     x
0   0      0      0      0   x     x
0   0      0      1      0   x     x
0   0      0      0      0   x     x
0   0      0      1      0   x     x
0   0      0      0      0   x     x
0   0      0      1      0   x     x
0   0      0      0      0   x     x
0   0      0      1      0   x     x
0   0      0      0      0   x     x
0   0      0      1      0   x     x
0   0      0      0      0   x     x
0   0      0      1      0   x     x
0   0      0      0      0   x     x
0   0      0      1      0   x     x
0   0      0      0      0   x     x
0   0      0      1      0   x     x
0   0      0      0      0   x     x
0   0      0      1      0   x     x
0   0      0      0      0   x     x
0   0      0      1      0   x     x
0   0      0      0      0   x     x
0   0      0      1      0   x     x
0   0      0      0      0   x     x
0   0      0      1      0   x     x
0   0      0      0      0   x     x
0   0      0      1      0   x     x
0   0      0      0      0   x     x
0   0      0      1      0   x     x
0   0      0      0      0   x     x
0   0      0      1      0   x     x
0   0      0      0      0   x     x
0   0      0      1      0   x     x
0   0      0      0      0   x     x
0   0      0      1      0   x     x
0   0      0      0      0   x     x
0   0      0      1      0   x     x
0   0      0      0      0   x     x
0   0      0      1      0   x     x
0   0      0      0      0   x     x
0   0      0      1      0   x     x
0   0      0      0      0   x     x
0   0      0      1      0   x     x
0   0      0      0      0   x     x
0   0      0      1      0   x     x
0   0      0      0      0   x     x
0   0      0      1      0   x     x
0   0      0      0      0   x     x
0   0      0      1      0   x     x
0   0      0      0      0   x     x
0   0      0      1      0   x     x
0   0      0      0      0   x     x
0   0      0      1      0   x     x
0   0      0      0      0   x     x
0   0      0      1      0   x     x
0   0      0      0      0   x     x
0   0      0      1      0   x     x
0   0      0      0      0   x     x
0   0      0      1      0   x     x
0   0      0      0      0   x     x
0   0      0      1      0   x     x
0   0      0      0      0   x     x
0   0      0      1      0   x     x
0   0      0      0      0   x     x
0   0      0      1      0   x     x
0   0      0      0      0   x     x
0   0      0      1      0   x     x
0   0      0      0      0   x     x
0   0      0      1      0   x     x
0   0      0      0      0   x     x
0   0      0      1      0   x     x
0   0      0      0      0   x     x
0   0      0      1      0   x     x
0   0      0      0      0   x     x
0   0      0      1      0   x     x
0   0      0      0      0   x     x
0   0      0      1      0   x     x
0   0      0      0      0   x     x
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*/
