// Digital circuit DigLo68_Exam2_3.dig as structural Verilog
module DigLo68_Exam2_3 (
  input  reset,
  input  [3:0] N,
  input  \new ,
  input  clock,
  output [7:0] num3,
  output [7:0] num5,
  output busy
);

  wire and_1_out, and_2_out, and_3_out, and_5_out, and_6_out, and_7_out, d_ff_1_q, en, equal_3, equal_5,
       new_once, new_reset, or_1_out;
  wire [3:0] multiplexer_1_out, n_val, r_3, r_5;
  wire [7:0] multiplexer_2_out, multiplexer_3_out, multiplexer_4_out, multiplexer_5_out, new_3, new_5;

  D_FF d_ff_1 (.D(\new ), .C(clock), .Q(d_ff_1_q));  // open: nQ
  and and_1 (and_1_out, ~d_ff_1_q, \new );  // And
  Multiplexer #(.Bits(4)) multiplexer_1 (.sel(reset), .in_0(N), .in_1(4'b0000), .out(multiplexer_1_out));
  and and_2 (and_2_out, equal_3, busy);
  Register #(.Bits(4)) register_1 (.D(multiplexer_1_out), .C(clock), .en(new_reset), .Q(n_val));
  Div #(.Bits(4)) div_1 (.a(n_val), .b(4'b0011), .r(r_3));  // open: q
  Multiplexer #(.Bits(8)) multiplexer_2 (.sel(and_2_out), .in_0({8{1'b0}}), .in_1(8'h1), .out(multiplexer_2_out));
  and and_3 (and_3_out, and_1_out, ~busy);  // And
  Div #(.Bits(4)) div_2 (.a(n_val), .b(4'b0101), .r(r_5));  // open: q
  Add #(.Bits(8)) add_1 (.a(num3), .b(multiplexer_2_out), .c_i(1'b0), .s(new_3));  // open: c_o
  and and_4 (new_once, and_3_out, ~reset);  // And
  Multiplexer #(.Bits(8)) multiplexer_3 (.sel(reset), .in_0(new_3), .in_1({8{1'b0}}), .out(multiplexer_3_out));
  Multiplexer #(.Bits(8)) multiplexer_4 (.sel(and_5_out), .in_0({8{1'b0}}), .in_1(8'h1), .out(multiplexer_4_out));
  and and_5 (and_5_out, equal_5, busy);
  Register #(.Bits(8)) register_2 (.D(multiplexer_3_out), .C(clock), .en(en), .Q(num3));
  or or_1 (or_1_out, new_once, busy);
  Comparator #(.Bits(4)) comparator_1 (.a(r_3), .b(4'b0000), .eq(equal_3));  // open: gt, lt
  Add #(.Bits(8)) add_2 (.a(num5), .b(multiplexer_4_out), .c_i(1'b0), .s(new_5));  // open: c_o
  and and_6 (and_6_out, or_1_out, ~busy);  // And
  or or_2 (new_reset, new_once, reset);
  Multiplexer #(.Bits(8)) multiplexer_5 (.sel(reset), .in_0(new_5), .in_1({8{1'b0}}), .out(multiplexer_5_out));
  Comparator #(.Bits(4)) comparator_2 (.a(r_5), .b(4'b0000), .eq(equal_5));  // open: gt, lt
  or or_3 (en, busy, new_reset);
  and and_7 (and_7_out, and_6_out, ~reset);  // And
  Register #(.Bits(8)) register_3 (.D(multiplexer_5_out), .C(clock), .en(en), .Q(num5));
  D_FF d_ff_2 (.D(and_7_out), .C(clock), .Q(busy));  // open: nQ

  // Other names for the same wires on the sheet: clk = clock
endmodule

/* Test case T01:
 N new reset clock num3 num5 busy 0 0 1 0 x x x 0 0 1 1 x x x 14 1 0 0 0 0 x 14 1 0 1 0 0 1 0 0 0 0 x x 1 0 0 0 1 x x x 0 0 0 0 x x x 0 0 0 1 x x x 0 0 0 0 x x x 0 0 0 1 x x x 0 0 0 0 x x x 0 0 0 1 x x x 0 0 0 0 x x x 0 0 0 1 x x x 0 0 0 0 x x x 0 0 0 1 x x x 0 0 0 0 x x x 0 0 0 1 x x x 0 0 0 0 x x x 0 0 0 1 x x x 0 0 0 0 x x x 0 0 0 1 x x x 0 0 0 0 x x x 0 0 0 1 x x x 0 0 0 0 0 0 0 0 0 0 1 0 0 0 15 1 0 0 0 0 x 15 1 0 1 0 0 1 0 0 0 0 x x 1 0 0 0 1 x x x 0 0 0 0 x x x 0 0 0 1 x x x 0 0 0 0 x x x 0 0 0 1 x x x 0 0 0 0 x x x 0 0 0 1 x x x 0 0 0 0 x x x 0 0 0 1 x x x 0 0 0 0 x x x 0 0 0 1 x x x 0 0 0 0 x x x 0 0 0 1 x x x 0 0 0 0 x x x 0 0 0 1 x x x 0 0 0 0 x x x 0 0 0 1 x x x 0 0 0 0 x x x 0 0 0 1 x x x 0 0 0 0 1 1 0 0 0 0 1 1 1 0 
*/
