// Digital circuit DigLo69_Exam1_2.dig as structural Verilog
module DigLo69_Exam1_2 (
  input  X3,
  input  X2,
  input  X1,
  input  X0,
  output Q2,
  output Q1,
  output Q0,
  output R1,
  output R0
);

  wire and_2_out, and_3_out, and_4_out, and_5_out, and_6_out, and_7_out, and_8_out, and_9_out, and_10_out,
       and_11_out, and_12_out, and_13_out, and_14_out, and_15_out, and_16_out, and_17_out, and_18_out, x0_t,
       x1_t, x2_t, x3_t;

  not not_1 (x3_t, X3);
  not not_2 (x2_t, X2);
  not not_3 (x1_t, X1);
  and and_1 (Q2, X2, X3);
  and and_2 (and_2_out, X1, X2, x3_t);
  and and_3 (and_3_out, x2_t, X3);
  and and_4 (and_4_out, X0, X1, x2_t);
  and and_5 (and_5_out, X0, x2_t, X3);
  and and_6 (and_6_out, X0, X1, X3);
  and and_7 (and_7_out, x1_t, X2, x3_t);
  and and_8 (and_8_out, X1, x2_t, X3);
  and and_9 (and_9_out, x0_t, X1, x2_t, x3_t);
  and and_10 (and_10_out, X0, x1_t, X2, x3_t);
  and and_11 (and_11_out, x0_t, x1_t, x2_t, X3);
  and and_12 (and_12_out, X0, X1, x2_t, X3);
  and and_13 (and_13_out, x0_t, X1, X2, X3);
  and and_14 (and_14_out, X0, x1_t, x2_t, x3_t);
  and and_15 (and_15_out, x0_t, x1_t, X2, x3_t);
  and and_16 (and_16_out, X0, X1, X2, x3_t);
  and and_17 (and_17_out, x0_t, X1, x2_t, X3);
  and and_18 (and_18_out, X0, x1_t, X2, X3);
  not not_4 (x0_t, X0);
  or or_1 (Q1, and_2_out, and_3_out);
  or or_2 (Q0, and_4_out, and_5_out, and_6_out, and_7_out, and_8_out);
  or or_3 (R1, and_9_out, and_10_out, and_11_out, and_12_out, and_13_out);
  or or_4 (R0, and_14_out, and_15_out, and_16_out, and_17_out, and_18_out);

  // Notes on the sheet:
  //   Q2: Quotient bit 2
  //   Q1: Quotient bit 1
  //   Q0: Quotient bit 0
  //   R1: Remainder bit 1
  //   R0: Remainder bit 0
  //   Don't change anything inside this box
endmodule

/* Test case T1:
X3 X2 X1 X0 Q2 Q1 Q0 R1 R0 0 0 0 0 0 0 0 0 0 0 1 1 1 0 1 0 0 1 1 1 1 1 1 0 1 0 0 
*/
