// Digital circuit DigLo69_Exam1_3.dig as structural Verilog
module DigLo69_Exam1_3 (
  input  CH,
  input  CL,
  input  MH,
  input  QL,
  input  MT,
  input  AD,
  output UP,
  output DN,
  output AL
);

  wire ad_t, and_1_out, and_2_out, and_3_out, and_4_out, and_5_out, and_6_out, and_7_out, and_8_out, ch_t,
       cl_t, high, mh_t, mt_t, not_7_out, ql_t;

  and and_1 (and_1_out, CH, MH);
  and and_2 (and_2_out, CH, QL);
  and and_3 (and_3_out, MH, QL);
  not not_1 (ch_t, CH);
  or or_1 (high, and_1_out, and_2_out, and_3_out);
  not not_2 (cl_t, CL);
  not not_3 (mh_t, MH);
  and and_4 (and_4_out, high, MT);
  not not_4 (ql_t, QL);
  and and_5 (and_5_out, high, mt_t);
  and and_6 (and_6_out, CL, mt_t);
  and and_7 (and_7_out, CH, MH, QL);
  and and_8 (and_8_out, and_4_out, ad_t);
  not not_5 (mt_t, MT);
  not not_6 (ad_t, AD);
  or or_2 (UP, and_5_out, AD);
  and and_9 (DN, and_6_out, not_7_out);
  not not_7 (not_7_out, UP);
  or or_3 (AL, and_7_out, and_8_out);

  // Notes on the sheet:
  //   UP: Scale Up
  //   DN: Scale Down
  //   AL: Alert
  //   Don't change anything inside this box
endmodule

/* Test case T1:
CH CL MH QL MT AD UP DN AL 
0 0 0 0 0 0 0 0 0 
1 0 0 1 0 0 1 0 0 
0 1 0 0 0 0 0 1 0 
1 0 1 1 0 0 1 0 1 
1 0 0 1 1 0 0 0 1 
0 0 0 0 0 1 1 0 0 
*/
