// Digital circuit DigLo69_Exam2_1.dig as structural Verilog
module DigLo69_Exam2_1 (
  input  reset,
  input  X,
  input  Y,
  input  Z,
  input  load,
  input  clock,
  output A,
  output B,
  output C
);

  wire and_1_out, and_2_out, and_3_out, and_4_out, and_6_out, multiplexer_1_out, multiplexer_2_out,
       multiplexer_3_out, or_1_out, or_2_out, or_3_out;

  and and_1 (and_1_out, ~A, ~B);  // And
  and and_2 (and_2_out, ~B, ~C);  // And
  and and_3 (and_3_out, B, ~C);  // And
  and and_4 (and_4_out, A, B);
  and and_5 (and_4_out, ~A, ~B, C);  // And
  and and_6 (and_6_out, B, ~C);  // And
  or or_1 (or_1_out, and_1_out, and_2_out);
  or or_2 (or_2_out, and_3_out, and_4_out, and_4_out);
  or or_3 (or_3_out, and_6_out, A);
  Multiplexer multiplexer_1 (.sel(load), .in_0(or_1_out), .in_1(X), .out(multiplexer_1_out));
  Multiplexer multiplexer_2 (.sel(load), .in_0(or_2_out), .in_1(Y), .out(multiplexer_2_out));
  Multiplexer multiplexer_3 (.sel(load), .in_0(or_3_out), .in_1(Z), .out(multiplexer_3_out));
  D_FF_AS d_ff_as_1 (.Set(reset), .D(multiplexer_1_out), .C(clock), .Clr(1'b0), .Q(A));  // open: nQ
  D_FF_AS d_ff_as_2 (.Set(1'b0), .D(multiplexer_2_out), .C(clock), .Clr(reset), .Q(B));  // open: nQ
  D_FF_AS d_ff_as_3 (.Set(reset), .D(multiplexer_3_out), .C(clock), .Clr(1'b0), .Q(C));  // open: nQ

  // Other names for the same wires on the sheet: clk = clock
endmodule

/* Test case T01:
X Y Z reset load clock A B C 
0 0 0 1 0 0 x x x 
0 0 0 1 0 1 1 0 1 
0 0 0 0 0 0 1 0 1 
0 0 0 0 0 1 0 0 1 
0 0 0 0 0 0 0 0 1 
0 0 0 0 0 1 1 1 0 
0 0 0 0 0 0 1 1 0 
0 0 0 0 0 1 0 1 1 
0 0 0 0 0 0 0 1 1 
0 0 0 0 0 1 0 0 0 
0 0 0 0 0 0 0 0 0 
1 1 0 0 1 0 0 0 0 
1 1 0 0 1 1 1 1 0 
1 1 0 0 1 0 1 1 0 
0 0 0 0 0 0 1 1 0 
0 0 0 0 0 1 0 1 1 
0 0 0 0 0 0 0 1 1 
0 0 0 0 0 1 0 0 0 
0 0 0 0 0 0 0 0 0 
0 0 0 0 0 1 1 0 0 
0 0 0 0 0 0 1 0 0 
0 0 0 1 0 0 1 0 1 
0 0 0 0 0 0 1 0 1 
0 0 0 0 0 1 0 0 1 
0 0 0 0 0 0 0 0 1 
0 0 0 0 0 1 1 1 0 
0 0 0 0 0 0 1 1 0 
0 0 0 0 0 1 0 1 1 
0 0 0 0 0 0 0 1 1 
0 0 0 0 0 1 0 0 0 
0 0 0 1 0 1 1 0 1 
0 0 0 0 0 1 1 0 1 
0 0 0 0 0 0 1 0 1 
0 0 0 0 0 1 0 0 1 
0 0 0 0 0 0 0 0 1 
0 0 0 0 0 1 1 1 0 
0 0 0 0 0 0 1 1 0 
0 0 0 0 0 1 0 1 1 
0 0 0 0 0 0 0 1 1 
0 0 0 0 0 1 0 0 0 
0 0 0 0 0 0 0 0 0 
0 0 0 0 0 1 1 0 0 
0 0 0 0 0 0 1 0 0 
0 0 0 0 0 1 1 0 1 
0 0 0 0 0 0 1 0 1
          
*/
