// Digital circuit DigLo69_Exam2_2.dig as structural Verilog
module DigLo69_Exam2_2 (
  input  [15:0] A,
  input  [15:0] D,
  input  [15:0] N,
  input  start,
  input  reset,
  input  clock,
  output [15:0] K,
  output [15:0] S,
  output busy
);

  wire and_1_out, and_2_out, and_3_out, and_6_out, and_8_out, and_9_out, and_10_out, d_ff_1_q, done, en,
       less, loop, or_1_out, or_2_out, set, start_once;
  wire [15:0] a_plus_d, a_val, d_val, k_plus_1, multiplexer_1_out, multiplexer_2_out, multiplexer_3_out,
       multiplexer_4_out, multiplexer_5_out, multiplexer_6_out, n_val, s_plus_a;

  D_FF d_ff_1 (.D(start), .C(clock), .Q(d_ff_1_q));  // open: nQ
  and and_1 (and_1_out, ~d_ff_1_q, start);  // And
  and and_2 (and_2_out, ~busy, and_1_out);  // And
  Multiplexer #(.Bits(16)) multiplexer_1 (.sel(set), .in_0(k_plus_1), .in_1({16{1'b0}}), .out(multiplexer_1_out));
  and and_3 (and_3_out, ~reset, and_2_out);  // And
  Multiplexer #(.Bits(16)) multiplexer_2 (
    .sel(reset), .in_0(multiplexer_1_out), .in_1({16{1'b0}}), .out(multiplexer_2_out));
  Add #(.Bits(16)) add_1 (.a(S), .b(a_val), .c_i(1'b0), .s(s_plus_a));  // open: c_o
  and and_4 (start_once, and_3_out, ~done);  // And
  Register #(.Bits(16)) register_1 (.D(multiplexer_2_out), .C(clock), .en(en), .Q(K));
  Add #(.Bits(16)) add_2 (.a(K), .b(16'h1), .c_i(1'b0), .s(k_plus_1));  // open: c_o
  and and_5 (set, ~busy, start_once);  // And
  and and_6 (and_6_out, ~busy, start_once);  // And
  Multiplexer #(.Bits(16)) multiplexer_3 (.sel(set), .in_0(s_plus_a), .in_1({16{1'b0}}), .out(multiplexer_3_out));
  Multiplexer #(.Bits(16)) multiplexer_4 (.sel(and_6_out), .in_0(a_plus_d), .in_1(A), .out(multiplexer_4_out));
  and and_7 (loop, busy, less);
  Multiplexer #(.Bits(16)) multiplexer_5 (
    .sel(reset), .in_0(multiplexer_3_out), .in_1({16{1'b0}}), .out(multiplexer_5_out));
  Comparator #(.Bits(16)) comparator_1 (.a(S), .b(n_val), .lt(less));  // open: gt, eq
  Multiplexer #(.Bits(16)) multiplexer_6 (
    .sel(reset), .in_0(multiplexer_4_out), .in_1({16{1'b0}}), .out(multiplexer_6_out));
  and and_8 (and_8_out, busy, ~less);  // And
  Register #(.Bits(16)) register_2 (.D(multiplexer_6_out), .C(clock), .en(en), .Q(a_val));
  or or_1 (or_1_out, loop, start_once);
  Register #(.Bits(16)) register_3 (.D(multiplexer_5_out), .C(clock), .en(en), .Q(S));
  or or_2 (or_2_out, and_8_out, done);
  Add #(.Bits(16)) add_3 (.a(a_val), .b(D), .c_i(1'b0), .s(a_plus_d));  // open: c_o
  and and_9 (and_9_out, or_2_out, ~reset);  // And
  and and_10 (and_10_out, or_1_out, ~reset);  // And
  Register #(.Bits(16)) register_4 (.D(D), .C(clock), .en(set), .Q(d_val));
  or or_3 (en, loop, start_once, reset);
  D_FF d_ff_2 (.D(and_10_out), .C(clock), .Q(busy));  // open: nQ
  D_FF d_ff_3 (.D(and_9_out), .C(clock), .Q(done));  // open: nQ
  Register #(.Bits(16)) register_5 (.D(N), .C(clock), .en(set), .Q(n_val));

  // Other names for the same wires on the sheet: clk = clock
endmodule

/* Test case T01:
A D N start reset clock K S busy
0 0 0 0 1 0 x x x
0 0 0 0 1 1 0 0 0
0 0 0 0 0 0 0 0 0
3 2 20 1 0 0 0 0 0
3 2 20 1 0 1 x x 1
3 2 20 0 0 0 x x x
3 2 20 0 0 1 x x x
3 2 20 0 0 0 x x x
3 2 20 0 0 1 x x x
3 2 20 0 0 0 x x x
3 2 20 0 0 1 x x x
3 2 20 0 0 0 x x x
3 2 20 0 0 1 x x x
3 2 20 0 0 0 x x x
3 2 20 0 0 1 x x x
3 2 20 0 0 0 x x x
3 2 20 0 0 1 x x x
3 2 20 0 0 0 x x x
3 2 20 0 0 1 x x x
3 2 20 0 0 0 x x x
3 2 20 0 0 1 x x x
3 2 20 0 0 0 x x x
3 2 20 0 0 1 x x x
3 2 20 0 0 0 x x x
3 2 20 0 0 1 x x x
3 2 20 0 0 0 x x x
3 2 20 0 0 1 x x x
3 2 20 0 0 0 x x x
3 2 20 0 0 1 x x x
3 2 20 0 0 0 x x x
3 2 20 0 0 1 x x x
3 2 20 0 0 0 x x x
3 2 20 0 0 1 x x x
3 2 20 0 0 0 x x x
3 2 20 0 0 1 x x x
3 2 20 0 0 0 x x x
3 2 20 0 0 1 x x x
3 2 20 0 0 0 x x x
3 2 20 0 0 1 x x x
3 2 20 0 0 0 x x x
3 2 20 0 0 1 x x x
3 2 20 0 0 0 x x x
3 2 20 0 0 1 x x x
3 2 20 0 0 0 x x x
3 2 20 0 0 1 x x x
3 2 20 0 0 0 x x x
3 2 20 0 0 1 x x x
3 2 20 0 0 0 x x x
3 2 20 0 0 1 4 24 0
3 2 20 0 0 0 4 24 0
3 2 20 0 0 1 4 24 0
3 2 20 0 0 0 4 24 0
4 3 97 0 0 0 4 24 0
4 3 97 0 0 1 4 24 0
4 3 97 0 0 0 4 24 0
4 3 97 1 0 0 4 24 0
4 3 97 1 0 1 4 24 0
4 3 97 0 0 0 4 24 0
4 3 97 0 0 1 4 24 0
4 3 97 0 0 0 4 24 0
4 3 97 0 0 1 4 24 0
4 3 97 0 0 0 4 24 0
4 3 97 0 0 1 4 24 0
4 3 97 0 0 0 4 24 0
4 3 97 0 1 0 x x x
4 3 97 0 1 1 0 0 0
4 3 97 0 0 0 0 0 0
5 3 60 1 0 0 0 0 0
5 3 60 1 0 1 x x 1
5 3 60 0 0 0 x x x
5 3 60 0 0 1 x x x
5 3 60 0 0 0 x x x
5 3 60 0 0 1 x x x
5 3 60 0 0 0 x x x
5 3 60 0 0 1 x x x
5 3 60 0 0 0 x x x
5 3 60 0 1 0 x x x
5 3 60 0 1 1 0 0 0
5 3 60 0 0 0 0 0 0
5 3 60 0 0 1 0 0 0
5 3 60 0 0 0 0 0 0
5 3 60 0 0 1 0 0 0
5 3 60 0 0 0 0 0 0
1 1 10 1 0 0 0 0 0
1 1 10 1 0 1 x x 1
1 1 10 0 0 0 x x x
1 1 10 0 0 1 x x x
1 1 10 0 0 0 x x x
1 1 10 0 0 1 x x x
1 1 10 0 0 0 x x x
1 1 10 0 0 1 x x x
1 1 10 0 0 0 x x x
1 1 10 0 0 1 x x x
1 1 10 0 0 0 x x x
1 1 10 0 0 1 x x x
1 1 10 0 0 0 x x x
1 1 10 0 0 1 x x x
1 1 10 0 0 0 x x x
1 1 10 0 0 1 x x x
1 1 10 0 0 0 x x x
1 1 10 0 0 1 x x x
1 1 10 0 0 0 x x x
1 1 10 0 0 1 x x x
1 1 10 0 0 0 x x x
1 1 10 0 0 1 x x x
1 1 10 0 0 0 x x x
1 1 10 0 0 1 x x x
1 1 10 0 0 0 x x x
1 1 10 0 0 1 x x x
1 1 10 0 0 0 x x x
1 1 10 0 0 1 x x x
1 1 10 0 0 0 x x x
1 1 10 0 0 1 x x x
1 1 10 0 0 0 x x x
1 1 10 0 0 1 x x x
1 1 10 0 0 0 x x x
1 1 10 0 0 1 x x x
1 1 10 0 0 0 x x x
1 1 10 0 0 1 x x x
1 1 10 0 0 0 x x x
1 1 10 0 0 1 x x x
1 1 10 0 0 0 x x x
1 1 10 0 0 1 x x x
1 1 10 0 0 0 x x x
1 1 10 0 0 1 x x x
1 1 10 0 0 0 x x x
1 1 10 0 0 1 x x x
1 1 10 0 0 0 x x x
1 1 10 0 0 1 4 10 0
1 1 10 0 0 0 4 10 0
1 1 10 0 0 1 4 10 0
1 1 10 0 0 0 4 10 0
          
*/
