// Digital circuit DigLo69_Exam2_3.dig as structural Verilog
module DigLo69_Exam2_3 (
  input  [7:0] N,
  input  \new ,
  input  reset,
  input  clock,
  output [7:0] ones,
  output [7:0] odd,
  output busy
);

  wire and_1_out, and_2_out, and_4_out, and_5_out, d_ff_1_q, en, or_1_out, set, start_once;
  wire [3:0] cnt_1;
  wire [7:0] multiplexer_1_out, multiplexer_2_out, multiplexer_3_out, multiplexer_4_out, multiplexer_5_out,
       n_val, new_odd, new_ones, ood_1;

  D_FF d_ff_1 (.D(\new ), .C(clock), .Q(d_ff_1_q));  // open: nQ
  and and_1 (and_1_out, ~d_ff_1_q, \new );  // And
  Multiplexer #(.Bits(8)) multiplexer_1 (.sel(reset), .in_0(N), .in_1({8{1'b0}}), .out(multiplexer_1_out));
  Register #(.Bits(8)) register_1 (.D(multiplexer_1_out), .C(clock), .en(set), .Q(n_val));
  BitCount #(.Bits(8)) bitcount_1 (.in(n_val), .out(cnt_1));
  Multiplexer #(.Bits(8)) multiplexer_2 (
    .sel(busy), .in_0({8{1'b0}}), .in_1({4'b0000, cnt_1}), .out(multiplexer_2_out));
  and and_2 (and_2_out, ~busy, and_1_out);  // And
  Add #(.Bits(8)) add_1 (.a(ones), .b(multiplexer_2_out), .c_i(1'b0), .s(new_ones));  // open: c_o
  and and_3 (start_once, ~reset, and_2_out);  // And
  Multiplexer #(.Bits(8)) multiplexer_3 (.sel(reset), .in_0(new_ones), .in_1({8{1'b0}}), .out(multiplexer_3_out));
  Multiplexer #(.Bits(8)) multiplexer_4 (.sel(busy), .in_0({8{1'b0}}), .in_1(ood_1), .out(multiplexer_4_out));
  Register #(.Bits(8)) register_2 (.D(multiplexer_3_out), .C(clock), .en(en), .Q(ones));
  Div #(.Bits(8)) div_1 (.a({4'b0000, cnt_1}), .b(8'h2), .r(ood_1));  // open: q
  Add #(.Bits(8)) add_2 (.a(odd), .b(multiplexer_4_out), .c_i(1'b0), .s(new_odd));  // open: c_o
  or or_1 (or_1_out, busy, start_once);
  Multiplexer #(.Bits(8)) multiplexer_5 (.sel(reset), .in_0(new_odd), .in_1({8{1'b0}}), .out(multiplexer_5_out));
  or or_2 (set, start_once, reset);
  Register #(.Bits(8)) register_3 (.D(multiplexer_5_out), .C(clock), .en(en), .Q(odd));
  or or_3 (en, busy, set);
  and and_4 (and_4_out, or_1_out, ~busy);  // And
  and and_5 (and_5_out, and_4_out, ~reset);  // And
  D_FF d_ff_2 (.D(and_5_out), .C(clock), .Q(busy));  // open: nQ

  // Other names for the same wires on the sheet: clk = clock; start = \new 
endmodule

/* Test case T01:
N new reset clock ones odd busy 0 0 1 0 x x x 0 0 1 1 0 0 0 0 0 0 0 0 0 0 5 1 0 0 0 0 0 5 1 0 1 x x 1 5 0 0 0 x x x 5 0 0 1 x x x 5 0 0 0 x x x 5 0 0 1 x x x 5 0 0 0 x x x 5 0 0 1 x x x 5 0 0 0 x x x 5 0 0 1 x x x 5 0 0 0 x x x 5 0 0 1 x x x 5 0 0 0 x x x 5 0 0 1 x x x 5 0 0 0 x x x 5 0 0 1 x x x 5 0 0 0 x x x 5 0 0 1 x x x 5 0 0 0 x x x 5 0 0 1 x x x 5 0 0 0 x x x 5 0 0 1 x x x 5 0 0 0 x x x 5 0 0 1 x x x 5 0 0 0 x x x 5 0 0 1 x x x 5 0 0 0 x x x 5 0 0 1 x x x 5 0 0 0 x x x 5 0 0 1 x x x 5 0 0 0 x x x 5 0 0 1 2 0 0 5 0 0 0 2 0 0 5 0 0 1 2 0 0 5 0 0 0 2 0 0 7 1 0 0 2 0 0 7 1 0 1 x x 1 7 0 0 0 x x x 7 0 0 1 x x x 7 0 0 0 x x x 7 0 0 1 x x x 7 0 0 0 x x x 7 0 0 1 x x x 7 0 0 0 x x x 7 0 0 1 x x x 7 0 0 0 x x x 7 0 0 1 x x x 7 0 0 0 x x x 7 0 0 1 x x x 7 0 0 0 x x x 7 0 0 1 x x x 7 0 0 0 x x x 7 0 0 1 x x x 7 0 0 0 x x x 7 0 0 1 x x x 7 0 0 0 x x x 7 0 0 1 x x x 7 0 0 0 x x x 7 0 0 1 x x x 7 0 0 0 x x x 7 0 0 1 x x x 7 0 0 0 x x x 7 0 0 1 x x x 7 0 0 0 x x x 7 0 0 1 x x x 7 0 0 0 x x x 7 0 0 1 5 1 0 7 0 0 0 5 1 0 7 0 0 1 5 1 0 7 0 0 0 5 1 0 255 1 0 0 5 1 0 255 1 0 1 x x 1 255 0 0 0 x x x 255 0 0 1 x x x 255 0 0 0 x x x 255 0 0 1 x x x 255 0 0 0 x x x 255 0 0 1 x x x 255 0 0 0 x x x 255 0 0 1 x x x 255 0 0 0 x x x 255 0 0 1 x x x 255 0 0 0 x x x 255 0 0 1 x x x 255 0 0 0 x x x 255 0 0 1 x x x 255 0 0 0 x x x 255 0 0 1 x x x 255 0 0 0 x x x 255 0 0 1 x x x 255 0 0 0 x x x 255 0 0 1 x x x 255 0 0 0 x x x 255 0 0 1 x x x 255 0 0 0 x x x 255 0 0 1 x x x 255 0 0 0 x x x 255 0 0 1 x x x 255 0 0 0 x x x 255 0 0 1 x x x 255 0 0 0 x x x 255 0 0 1 13 1 0 255 0 0 0 13 1 0 255 0 0 1 13 1 0 255 0 0 0 13 1 0 0 1 0 0 13 1 0 0 1 0 1 x x 1 0 0 0 0 x x x 0 0 0 1 x x x 0 0 0 0 x x x 0 0 0 1 x x x 0 0 0 0 x x x 0 0 0 1 x x x 0 0 0 0 x x x 0 0 0 1 x x x 0 0 0 0 x x x 0 0 0 1 x x x 0 0 0 0 x x x 0 0 0 1 x x x 0 0 0 0 x x x 0 0 0 1 x x x 0 0 0 0 x x x 0 0 0 1 x x x 0 0 0 0 x x x 0 0 0 1 x x x 0 0 0 0 x x x 0 0 0 1 x x x 0 0 0 0 x x x 0 0 0 1 x x x 0 0 0 0 x x x 0 0 0 1 x x x 0 0 0 0 x x x 0 0 0 1 x x x 0 0 0 0 x x x 0 0 0 1 x x x 0 0 0 0 x x x 0 0 0 1 13 1 0 0 0 0 0 13 1 0 0 0 0 1 13 1 0 0 0 0 0 13 1 0 128 1 0 0 13 1 0 128 1 0 1 x x 1 128 0 0 0 x x x 128 0 0 1 x x x 128 0 0 0 x x x 128 0 0 1 x x x 128 0 0 0 x x x 128 0 0 1 x x x 128 0 0 0 x x x 128 0 0 1 x x x 128 0 0 0 x x x 128 0 0 1 x x x 128 0 0 0 x x x 128 0 0 1 x x x 128 0 0 0 x x x 128 0 0 1 x x x 128 0 0 0 x x x 128 0 0 1 x x x 128 0 0 0 x x x 128 0 0 1 x x x 128 0 0 0 x x x 128 0 0 1 x x x 128 0 0 0 x x x 128 0 0 1 x x x 128 0 0 0 x x x 128 0 0 1 x x x 128 0 0 0 x x x 128 0 0 1 x x x 128 0 0 0 x x x 128 0 0 1 x x x 128 0 0 0 x x x 128 0 0 1 14 2 0 128 0 0 0 14 2 0 128 0 0 1 14 2 0 128 0 0 0 14 2 0 6 1 0 0 14 2 0 6 1 0 1 x x 1 6 0 0 0 x x x 6 0 0 1 x x x 6 0 0 0 x x x 6 0 0 1 x x x 6 0 0 0 x x x 6 0 0 1 x x x 6 0 0 0 x x x 6 0 0 1 x x x 6 0 0 0 x x x 6 0 0 1 x x x 6 0 0 0 x x x 6 0 0 1 x x x 6 0 0 0 x x x 6 0 0 1 x x x 6 0 0 0 x x x 6 0 0 1 x x x 6 0 0 0 x x x 6 0 0 1 x x x 6 0 0 0 x x x 6 0 0 1 x x x 6 0 0 0 x x x 6 0 0 1 x x x 6 0 0 0 x x x 6 0 0 1 x x x 6 0 0 0 x x x 6 0 0 1 x x x 6 0 0 0 x x x 6 0 0 1 x x x 6 0 0 0 x x x 6 0 0 1 16 2 0 6 0 0 0 16 2 0 6 0 0 1 16 2 0 6 0 0 0 16 2 0 200 1 0 0 16 2 0 200 1 0 1 x x 1 200 0 0 0 x x x 200 0 0 1 x x x 200 0 0 0 x x x 200 0 0 1 x x x 200 0 0 0 x x x 200 0 0 1 x x x 200 0 0 0 x x x 200 0 1 0 x x x 200 0 1 1 0 0 0 200 0 0 0 0 0 0 200 0 0 1 0 0 0 200 0 0 0 0 0 0 200 0 0 1 0 0 0 200 0 0 0 0 0 0 15 1 0 0 0 0 0 15 1 0 1 x x 1 15 0 0 0 x x x 15 0 0 1 x x x 15 0 0 0 x x x 15 0 0 1 x x x 15 0 0 0 x x x 15 0 0 1 x x x 15 0 0 0 x x x 15 0 0 1 x x x 15 0 0 0 x x x 15 0 0 1 x x x 15 0 0 0 x x x 15 0 0 1 x x x 15 0 0 0 x x x 15 0 0 1 x x x 15 0 0 0 x x x 15 0 0 1 x x x 15 0 0 0 x x x 15 0 0 1 x x x 15 0 0 0 x x x 15 0 0 1 x x x 15 0 0 0 x x x 15 0 0 1 x x x 15 0 0 0 x x x 15 0 0 1 x x x 15 0 0 0 x x x 15 0 0 1 x x x 15 0 0 0 x x x 15 0 0 1 x x x 15 0 0 0 x x x 15 0 0 1 4 0 0 15 0 0 0 4 0 0 15 0 0 1 4 0 0 15 0 0 0 4 0 0 1 1 0 0 4 0 0 1 1 0 1 x x 1 1 0 0 0 x x x 1 0
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*/
