// Digital circuit DigLo_Lab.dig as structural Verilog
module DigLo_Lab (
  input  A,
  input  B,
  input  Cin,
  output Sum,
  output Cout
);

  wire n1, n2, n3, n4, n5, n6, sum1;

  _7400 _7400_1 (
    .pin1(A), .pin2(B), .pin3(n1), .pin4(A), .pin5(n1), .pin6(n2), .pin7(1'b0), .pin8(n3), .pin9(B),
    .pin10(n1), .pin11(sum1), .pin12(n2), .pin13(n3), .pin14(1'b1));
  _7400 _7400_2 (
    .pin1(sum1), .pin2(Cin), .pin3(n4), .pin4(sum1), .pin5(n4), .pin6(n5), .pin7(1'b0), .pin8(n6),
    .pin9(Cin), .pin10(n4), .pin11(Sum), .pin12(n5), .pin13(n6), .pin14(1'b1));
  _7400 _7400_3 (
    .pin1(n1), .pin2(n4), .pin3(Cout), .pin4(1'b0), .pin5(1'b0), .pin7(1'b0), .pin9(1'b0), .pin10(1'b0),
    .pin12(1'b0), .pin13(1'b0), .pin14(1'b1));  // open: pin6, pin8, pin11
endmodule
