// Digital circuit act2_6.dig as structural Verilog
module act2_6 (
  input  A,
  input  B,
  input  C,
  input  D,
  output Z1,
  output Z2,
  output Z3
);

  wire not_1_out, not_2_out, not_3_out, not_4_out, not_5_out, not_6_out, not_7_out, not_8_out, not_9_out,
       not_10_out, not_11_out, not_12_out, not_13_out, not_14_out, or_1_out, or_2_out, or_3_out, or_4_out,
       or_5_out, or_6_out, or_7_out, or_8_out, or_9_out, or_10_out, or_11_out, or_12_out, or_13_out,
       or_14_out;

  not not_1 (not_1_out, D);
  not not_2 (not_2_out, C);
  not not_3 (not_3_out, C);
  not not_4 (not_4_out, D);
  not not_5 (not_5_out, C);
  or or_1 (or_1_out, A, B);
  or or_2 (or_2_out, A, not_1_out);
  or or_3 (or_3_out, B, not_2_out);
  or or_4 (or_4_out, not_3_out, not_4_out);
  or or_5 (or_5_out, A, not_5_out);
  and and_1 (Z1, or_1_out, or_2_out, or_3_out, or_4_out, or_5_out);
  or or_6 (or_6_out, not_6_out, not_7_out);
  not not_6 (not_6_out, A);
  not not_7 (not_7_out, B);
  not not_8 (not_8_out, A);
  or or_7 (or_7_out, not_8_out, D);
  not not_9 (not_9_out, B);
  or or_8 (or_8_out, not_9_out, C);
  or or_9 (or_9_out, C, D);
  or or_10 (or_10_out, not_10_out, C);
  not not_10 (not_10_out, A);
  and and_2 (Z2, or_6_out, or_7_out, or_8_out, or_9_out, or_10_out);
  or or_11 (or_11_out, not_11_out, C);
  not not_11 (not_11_out, A);
  or or_12 (or_12_out, A, not_12_out);
  not not_12 (not_12_out, C);
  not not_13 (not_13_out, B);
  or or_13 (or_13_out, not_13_out, D);
  or or_14 (or_14_out, B, not_14_out);
  not not_14 (not_14_out, D);
  and and_3 (Z3, or_11_out, or_12_out, or_13_out, or_14_out);
endmodule
