// Digital circuit act2_9.dig as structural Verilog
module act2_9 (
  input  X0,
  input  X1,
  input  S1,
  input  X2,
  input  X3,
  input  S0,
  output Z
);

  wire and_1_out, and_2_out, and_3_out, and_4_out, not_1_out, not_2_out, not_3_out, not_4_out;

  and and_1 (and_1_out, X0, not_1_out, not_2_out);
  not not_1 (not_1_out, S1);
  not not_2 (not_2_out, S0);
  and and_2 (and_2_out, X1, not_3_out, S0);
  not not_3 (not_3_out, S1);
  and and_3 (and_3_out, X2, S1, not_4_out);
  not not_4 (not_4_out, S0);
  and and_4 (and_4_out, X3, S1, S0);
  or or_1 (Z, and_1_out, and_2_out, and_3_out, and_4_out);

  // Other names for the same wires on the sheet: s2 = S0
endmodule
