// Digital circuit act3_1.dig as structural Verilog
module act3_1 (
  input  [3:0] In,
  output C,
  output D,
  output E,
  output F,
  output G,
  output A,
  output B
);

  wire and_1_out, and_2_out, and_3_out, and_4_out, and_5_out, and_6_out, and_7_out, and_8_out, and_9_out,
       and_10_out, and_11_out, and_12_out, and_13_out, and_14_out, and_15_out, and_16_out, and_17_out, i0_t,
       i1_t, i2_t, i3_t, not_5_out, not_6_out, not_7_out, not_8_out, not_9_out, not_10_out, not_11_out,
       not_12_out, or_2_out, or_3_out, or_5_out, xor_1_out;

  not not_1 (i3_t, In[3]);
  not not_2 (i0_t, In[0]);
  not not_3 (i1_t, In[1]);
  not not_4 (i2_t, In[2]);
  and and_1 (and_1_out, In[1], In[0]);
  not not_5 (not_5_out, In[2]);
  and and_2 (and_2_out, not_5_out, not_6_out);
  not not_6 (not_6_out, In[0]);
  and and_3 (and_3_out, In[1], not_7_out);
  not not_7 (not_7_out, In[0]);
  and and_4 (and_4_out, In[2], not_8_out, In[0]);
  not not_8 (not_8_out, In[1]);
  not not_9 (not_9_out, In[2]);
  and and_5 (and_5_out, not_9_out, In[0]);
  not not_10 (not_10_out, In[2]);
  and and_6 (and_6_out, not_10_out, In[1]);
  and and_7 (and_7_out, In[0], In[1]);
  and and_8 (and_8_out, not_11_out, not_12_out);
  not not_11 (not_11_out, In[0]);
  not not_12 (not_12_out, In[1]);
  and and_9 (and_9_out, i2_t, i0_t);
  and and_10 (and_10_out, In[1], i0_t);
  and and_11 (and_11_out, i2_t, In[1]);
  and and_12 (and_12_out, In[2], i1_t, In[0]);
  and and_13 (and_13_out, i1_t, i0_t);
  and and_14 (and_14_out, i3_t, In[2]);
  xor xor_1 (xor_1_out, In[2], In[1]);
  and and_15 (and_15_out, In[1], i0_t);
  and and_16 (and_16_out, i0_t, i2_t);
  and and_17 (and_17_out, i0_t, In[1]);
  or or_1 (C, In[2], i1_t, In[0]);
  or or_2 (or_2_out, and_9_out, In[3], and_10_out);
  or or_3 (or_3_out, and_11_out, and_12_out);
  or or_4 (E, and_16_out, and_17_out);
  or or_5 (or_5_out, In[3], and_13_out);
  or or_6 (G, In[3], xor_1_out, and_15_out);
  or or_7 (A, and_2_out, and_3_out, and_1_out, and_4_out, In[3]);
  or or_8 (B, and_5_out, and_6_out, and_7_out, and_8_out);
  or or_9 (D, or_2_out, or_3_out);
  or or_10 (F, or_5_out, and_14_out);
  Seven_Seg seven_seg_1 (.a(A), .b(B), .c(C), .d(D), .e(E), .f(F), .g(G), .dp(1'b0));

  // Other names for the same wires on the sheet: i0 = In[0]; i1 = In[1]; i2 = In[2]; i3 = In[3]
endmodule
