// Digital circuit act3_2.dig as structural Verilog
module act3_2 (
  input  [2:0] In,
  output [7:0] Z
);

  wire and_2_out, and_3_out, and_4_out, and_5_out, and_6_out, and_7_out, AxB, AxC, m7, not_A, not_B, not_C;

  not not_1 (not_C, In[0]);
  not not_2 (not_B, In[1]);
  not not_3 (not_A, In[2]);
  xor xor_1 (AxB, In[2], In[1]);
  xor xor_2 (AxC, In[2], In[0]);
  and and_1 (m7, In[2], In[1], In[0]);
  and and_2 (and_2_out, In[1], not_C);
  and and_3 (and_3_out, not_B, AxC);
  and and_4 (and_4_out, AxB, not_C);
  and and_5 (and_5_out, not_B, not_C);
  and and_6 (and_6_out, not_A, In[0]);
  and and_7 (and_7_out, In[2], not_B);
  or or_1 (Z[0], and_2_out, and_3_out);
  or or_2 (Z[1], and_4_out, m7);
  or or_3 (Z[2], and_5_out, AxB);
  or or_4 (Z[3], and_6_out, and_7_out);
  or or_5 (Z[5], Z[0], m7);

  assign {Z[7:6], Z[4]} = 3'b010;

  // Other names for the same wires on the sheet: C = In[0]; B = In[1]; A = In[2]
endmodule
