// Digital circuit act3_3.dig as structural Verilog
module act3_3 (
  input  [3:0] In,
  input  [1:0] Selector,
  output [3:0] Output
);

  wire A1, A2, A3, and_8_out, and_9_out, and_10_out, and_11_out, and_12_out, and_13_out, and_14_out,
       and_15_out, and_16_out, and_17_out, and_18_out, and_19_out, and_20_out, and_21_out, and_22_out,
       and_23_out, and_24_out, and_25_out, and_26_out, and_27_out, C0, C1, C2, E0, E1, E2, N1, N2, N3,
       not_s0, not_s1, not_x, not_y, or_3_out, or_10_out, or_11_out, or_12_out, or_13_out, or_14_out,
       or_15_out, or_16_out, or_17_out, sel0, sel1, sel2, sel3, term_xprimeyprimez, term_xy, term_xyprimez,
       term_xyz, term_yz;

  not not_1 (E0, In[0]);
  not not_2 (not_y, In[1]);
  not not_3 (not_x, In[2]);
  not not_4 (not_s0, Selector[0]);
  not not_5 (not_s1, Selector[1]);
  or or_1 (term_yz, In[1], In[0]);
  or or_2 (term_xy, In[2], In[1]);
  and and_1 (sel0, not_s1, not_s0);
  and and_2 (sel1, not_s1, Selector[0]);
  and and_3 (sel2, Selector[1], not_s0);
  and and_4 (sel3, Selector[1], Selector[0]);
  or or_3 (or_3_out, In[1], E0);
  and and_5 (term_xyprimez, In[2], not_y, In[0]);
  and and_6 (term_xprimeyprimez, not_x, not_y, In[0]);
  and and_7 (term_xyz, In[2], or_3_out);
  and and_8 (and_8_out, not_x, In[1]);
  and and_9 (and_9_out, In[1], E0);
  xnor xnor_1 (E1, In[1], In[0]);
  xor xor_1 (E2, In[2], term_yz);
  and and_10 (and_10_out, In[2], term_yz);
  xor xor_2 (C0, In[1], In[0]);
  xor xor_3 (C1, In[2], In[1]);
  xor xor_4 (C2, In[3], In[2]);
  or or_4 (A1, In[3], and_8_out, term_xyprimez);
  or or_5 (A2, In[3], term_xyz);
  or or_6 (N1, In[3], and_9_out, term_xyprimez);
  or or_7 (N2, term_xyz, term_xprimeyprimez);
  and and_11 (and_11_out, In[0], term_xy);
  or or_8 (A3, In[3], and_10_out);
  or or_9 (N3, In[3], and_11_out);
  and and_12 (and_12_out, E0, sel0);
  and and_13 (and_13_out, C0, sel1);
  and and_14 (and_14_out, In[0], sel2);
  and and_15 (and_15_out, In[0], sel3);
  and and_16 (and_16_out, E1, sel0);
  and and_17 (and_17_out, C1, sel1);
  and and_18 (and_18_out, A1, sel2);
  and and_19 (and_19_out, N1, sel3);
  and and_20 (and_20_out, E2, sel0);
  and and_21 (and_21_out, C2, sel1);
  and and_22 (and_22_out, A2, sel2);
  and and_23 (and_23_out, N2, sel3);
  and and_24 (and_24_out, A3, sel0);
  and and_25 (and_25_out, In[3], sel1);
  and and_26 (and_26_out, A3, sel2);
  and and_27 (and_27_out, N3, sel3);
  or or_10 (or_10_out, and_12_out, and_13_out);
  or or_11 (or_11_out, and_14_out, and_15_out);
  or or_12 (or_12_out, and_16_out, and_17_out);
  or or_13 (or_13_out, and_18_out, and_19_out);
  or or_14 (or_14_out, and_20_out, and_21_out);
  or or_15 (or_15_out, and_22_out, and_23_out);
  or or_16 (or_16_out, and_24_out, and_25_out);
  or or_17 (or_17_out, and_26_out, and_27_out);
  or or_18 (Output[0], or_10_out, or_11_out);
  or or_19 (Output[1], or_12_out, or_13_out);
  or or_20 (Output[2], or_14_out, or_15_out);
  or or_21 (Output[3], or_16_out, or_17_out);

  // Other names for the same wires on the sheet: E3 = A3; A0 = In[0]; N0 = In[0]; z = In[0]; y = In[1]; x = In[2];
  //   C3 = In[3]; w = In[3]; not_z = E0; Out_0 = Output[0]; Out_1 = Output[1]; Out_2 = Output[2]; Out_3 = Output[3];
  //   s0 = Selector[0]; s1 = Selector[1]
endmodule
