// Digital circuit act3_4.dig as structural Verilog
module act3_4 (
  input  [6:0] In,
  output [6:0] Output
);

  wire and_1_out, and_2_out, and_3_out, and_4_out, and_5_out, and_6_out, and_7_out, not_s1, not_s2, not_s3,
       s1, s2, s3, xor_1_out, xor_2_out, xor_3_out, xor_4_out, xor_5_out, xor_6_out;

  xor xor_1 (xor_1_out, In[6], In[4]);
  xor xor_2 (xor_2_out, In[2], In[0]);
  xor xor_3 (xor_3_out, In[5], In[4]);
  xor xor_4 (xor_4_out, In[1], In[0]);
  xor xor_5 (xor_5_out, In[3], In[2]);
  xor xor_6 (xor_6_out, In[1], In[0]);
  xor xor_7 (s1, xor_1_out, xor_2_out);
  xor xor_8 (s2, xor_3_out, xor_4_out);
  xor xor_9 (s3, xor_5_out, xor_6_out);
  not not_1 (not_s1, s1);
  not not_2 (not_s2, s2);
  not not_3 (not_s3, s3);
  and and_1 (and_1_out, not_s3, not_s2, s1);
  and and_2 (and_2_out, not_s3, s2, not_s1);
  and and_3 (and_3_out, not_s3, s2, s1);
  and and_4 (and_4_out, s3, not_s2, not_s1);
  and and_5 (and_5_out, s3, not_s2, s1);
  and and_6 (and_6_out, s3, s2, not_s1);
  and and_7 (and_7_out, s3, s2, s1);
  xor xor_10 (Output[6], and_1_out, In[6]);
  xor xor_11 (Output[5], and_2_out, In[5]);
  xor xor_12 (Output[4], and_3_out, In[4]);
  xor xor_13 (Output[3], and_4_out, In[3]);
  xor xor_14 (Output[2], and_5_out, In[2]);
  xor xor_15 (Output[1], and_6_out, In[1]);
  xor xor_16 (Output[0], and_7_out, In[0]);

  // Other names for the same wires on the sheet: c1 = Output[6]; c2 = Output[5]; c3 = Output[4]; c4 = Output[3];
  //   c5 = Output[2]; c6 = Output[1]; c7 = Output[0]; p7 = In[0]; p6 = In[1]; p5 = In[2]; p4 = In[3]; p3 = In[4];
  //   p2 = In[5]; p1 = In[6]
endmodule
