// Digital circuit act4_1.dig as structural Verilog
module act4_1 (
  input  A,
  input  B,
  input  C,
  input  D,
  output After,
  output [4:0] CheckGlitch,
  output Before
);

  wire and_1_out, and_2_out, and_3_out, and_4_out, and_5_out;

  and and_1 (and_1_out, ~C, D);  // And
  and and_2 (and_2_out, A, ~B, D);  // And
  and and_3 (and_3_out, ~C, D);  // And
  and and_4 (and_4_out, A, ~B, D);  // And
  and and_5 (and_5_out, ~B, D);  // And
  or or_1 (Before, ~A, and_1_out, and_2_out);  // Or
  or or_2 (After, ~A, and_3_out, and_4_out, and_5_out);  // Or
  Counter #(.Bits(5)) counter_1 (.en(1'b1), .C(After), .clr(1'b0), .out(CheckGlitch));  // open: ovf

  // Notes on the sheet:
  //   Must not change this section
endmodule

/* Test case T1:
A B C D Before After CheckGlitch
0 0 0 0 1 1 1
0 0 0 1 1 1 1
0 0 1 1 1 1 1
1 0 1 1 1 1 1
0 0 1 1 1 1 1
1 0 1 1 1 1 1
0 0 1 1 1 1 1
*/
