// Digital circuit act6_2.dig as structural Verilog
module act6_2 (
  input  reset,
  input  X,
  input  Y,
  input  Z,
  input  load,
  input  clock,
  output C,
  output B,
  output A
);

  wire a_t, and_1_out, and_2_out, and_3_out, and_4_out, and_5_out, and_6_out, b_t, c_t, multiplexer_1_out,
       multiplexer_2_out, multiplexer_3_out, not_1_out, not_2_out, not_3_out, or_1_out, or_2_out, xor_1_out;

  and and_1 (and_1_out, A, C);
  and and_2 (and_2_out, A, b_t);
  and and_3 (and_3_out, A, B);
  or or_1 (or_1_out, B, and_1_out);
  or or_2 (or_2_out, c_t, and_2_out);
  xor xor_1 (xor_1_out, C, and_3_out);
  Multiplexer multiplexer_1 (.sel(load), .in_0(or_1_out), .in_1(Z), .out(multiplexer_1_out));
  Multiplexer multiplexer_2 (.sel(load), .in_0(or_2_out), .in_1(Y), .out(multiplexer_2_out));
  Multiplexer multiplexer_3 (.sel(load), .in_0(xor_1_out), .in_1(X), .out(multiplexer_3_out));
  not not_1 (not_1_out, reset);
  and and_4 (and_4_out, not_1_out, multiplexer_1_out);
  not not_2 (not_2_out, reset);
  and and_5 (and_5_out, not_2_out, multiplexer_2_out);
  not not_3 (not_3_out, reset);
  and and_6 (and_6_out, not_3_out, multiplexer_3_out);
  D_FF d_ff_1 (.D(and_4_out), .C(clock), .Q(C), .nQ(c_t));
  D_FF d_ff_2 (.D(and_5_out), .C(clock), .Q(B), .nQ(b_t));
  D_FF d_ff_3 (.D(and_6_out), .C(clock), .Q(A), .nQ(a_t));

  // Other names for the same wires on the sheet: clk = clock
endmodule

/* Test case T06:
X Y Z reset load clock A B C 0 0 0 1 0 0 x x x 0 0 0 1 0 1 0 0 0 1 1 0 0 1 0 0 0 0 1 1 0 0 1 1 1 1 0 0 0 0 0 0 0 1 1 0 0 0 0 0 0 1 1 1 1 0 0 0 0 0 0 1 1 1 0 0 0 0 0 1 0 0 1 0 0 0 0 0 0 0 0 1 0 0 0 0 0 1 1 0 0 0 0 0 0 0 0 1 0 0 0 0 0 0 0 1 0 1 0 0 0 0 0 0 0 0 1 0 0 0 0 0 0 1 0 1 1 0 0 0 0 0 0 0 1 1 0 0 0 0 0 1 1 0 1 0 0 0 0 0 0 1 0 1 0 0 0 0 0 1 1 1 1 0 0 0 0 0 0 1 1 1 0 0 0 0 0 1 0 0 1 0 0 0 0 0 0 0 0 1 
*/
