// Digital circuit act6_3.dig as structural Verilog
module act6_3 (
  input  reset,
  input  [1:0] Coin,
  input  clock,
  output Open,
  output [3:0] Change
);

  wire and_1_out, coin_0, coin_2, coin_5, coin_10, d0, d1, m1, m2, m3, m4, m5, n_rst, nc0, nc1, nq0, nq1,
       or_2_out, or_3_out, or_4_out, or_5_out, or_8_out, or_9_out, or_10_out, or_11_out, or_12_out, q0, q1,
       q1_or_q0, state_0, state_2, state_4, state_5, t_c2_or_c10, t_ch0_a, t_ch0_b, t_ch1_a, t_ch1_b,
       t_ch2_a, t_ch2_b, t_open1, t_open2, t_s2_or_s4;

  not not_1 (n_rst, reset);
  not not_2 (nq1, q1);
  not not_3 (nq0, q0);
  not not_4 (nc1, Coin[1]);
  not not_5 (nc0, Coin[0]);
  or or_1 (q1_or_q0, q1, q0);
  and and_1 (and_1_out, q1, coin_10);
  and and_2 (t_ch1_a, state_2, coin_10);
  and and_3 (t_ch1_b, state_4, coin_5);
  and and_4 (Change[3], and_1_out, n_rst);
  and and_5 (t_open1, q1_or_q0, coin_5);
  and and_6 (t_open2, q1, coin_2);
  or or_2 (or_2_out, t_ch1_a, t_ch1_b);
  and and_7 (coin_0, nc1, nc0);
  and and_8 (coin_2, nc1, Coin[0]);
  and and_9 (coin_5, Coin[1], nc0);
  and and_10 (coin_10, Coin[1], Coin[0]);
  and and_11 (Change[1], or_2_out, n_rst);
  and and_12 (t_ch2_a, nq1, coin_10);
  and and_13 (t_ch2_b, state_5, coin_5);
  or or_3 (or_3_out, coin_10, t_open1);
  and and_14 (state_0, nq1, nq0);
  and and_15 (state_2, nq1, q0);
  and and_16 (state_4, q1, nq0);
  and and_17 (state_5, q1, q0);
  or or_4 (or_4_out, or_3_out, t_open2);
  or or_5 (or_5_out, t_ch2_a, t_ch2_b);
  or or_6 (t_s2_or_s4, state_2, state_4);
  or or_7 (t_c2_or_c10, coin_2, coin_10);
  and and_18 (Open, or_4_out, n_rst);
  and and_19 (Change[2], or_5_out, n_rst);
  and and_20 (m1, state_0, coin_5);
  and and_21 (m2, state_2, coin_2);
  and and_22 (m3, q1, coin_0);
  and and_23 (m4, state_0, coin_2);
  and and_24 (m5, q0, coin_0);
  and and_25 (t_ch0_a, t_s2_or_s4, coin_5);
  and and_26 (t_ch0_b, state_5, t_c2_or_c10);
  or or_8 (or_8_out, m1, m2);
  or or_9 (or_9_out, m4, m1);
  D_FF d_ff_1 (.D(d1), .C(clock), .Q(q1));  // open: nQ
  D_FF d_ff_2 (.D(d0), .C(clock), .Q(q0));  // open: nQ
  or or_10 (or_10_out, t_ch0_a, t_ch0_b);
  or or_11 (or_11_out, or_8_out, m3);
  or or_12 (or_12_out, or_9_out, m5);
  and and_27 (Change[0], or_10_out, n_rst);
  and and_28 (d1, or_11_out, n_rst);
  and and_29 (d0, or_12_out, n_rst);

  // Other names for the same wires on the sheet: ch0 = Change[0]; ch1 = Change[1]; ch2 = Change[2]; ch3 = Change[3];
  //   clk = clock; c0 = Coin[0]; c1 = Coin[1]; open_out = Open
endmodule

/* Test case T14:
reset Coin clock Open Change 1 0 0 x x 1 0 1 x x 1 0 0 0 0 1 0 1 x x 1 0 0 0 0 1 0 1 x x 1 0 0 0 0 1 0 1 x x 0 0 0 0 0 0 0 1 x x 0 0 0 0 0 0 0 1 x x 0 0 0 0 0 0 0 1 x x 0 0 0 0 0 0 0 1 x x 0 0 0 0 0 0 0 1 x x 0 0 0 0 0 0 0 1 x x 0 1 0 0 0 0 1 1 x x 0 1 0 0 0 0 1 1 x x 0 2 0 1 3 0 2 1 x x 0 0 0 0 0 0 0 1 x x 0 0 0 0 0 0 0 1 x x 0 0 0 0 0 0 0 1 x x 0 0 0 0 0 0 0 1 x x 1 0 0 0 0 1 0 1 x x 1 0 0 0 0 1 0 1 x x 0 0 0 0 0 0 0 1 x x 0 0 0 0 0 0 0 1 x x 0 2 0 0 0 0 2 1 x x 0 3 0 1 9 0 3 1 x x 0 0 0 0 0 0 0 1 x x 
*/

/* Test case T12:
reset Coin clock Open Change 1 0 0 x x 1 0 1 x x 0 1 0 0 0 0 1 1 x x 1 0 0 0 0 1 0 1 x x 0 0 0 0 0 0 0 1 x x 0 1 0 0 0 0 1 1 x x 0 1 0 0 0 0 1 1 x x 1 0 0 0 0 1 0 1 x x 0 0 0 0 0 0 0 1 x x 0 2 0 0 0 0 2 1 x x 1 0 0 0 0 1 0 1 x x 0 0 0 0 0 0 0 1 x x 0 1 0 0 0 0 1 1 x x 0 1 0 0 0 0 1 1 x x 0 1 0 1 0 0 1 1 x x 0 0 0 0 0 0 0 1 x x 0 2 0 0 0 0 2 1 x x 0 0 0 0 0 0 0 1 x x 1 0 0 0 0 1 0 1 x x 0 3 0 1 4 0 3 1 x x 0 0 0 0 0 0 0 1 x x 
*/

/* Test case T10:
reset Coin clock Open Change 1 0 0 x x 1 0 1 x x 0 0 0 0 0 0 0 1 x x 0 0 0 0 0 0 0 1 x x 0 1 0 0 0 0 1 1 x x 0 0 0 0 0 0 0 1 x x 0 0 0 0 0 0 0 1 x x 0 1 0 0 0 0 1 1 x x 0 0 0 0 0 0 0 1 x x 0 0 0 0 0 0 0 1 x x 0 0 0 0 0 0 0 1 x x 0 2 0 1 3 0 2 1 x x 0 0 0 0 0 0 0 1 x x 0 0 0 0 0 0 0 1 x x 0 2 0 0 0 0 2 1 x x 0 0 0 0 0 0 0 1 x x 0 0 0 0 0 0 0 1 x x 0 3 0 1 9 0 3 1 x x 0 0 0 0 0 0 0 1 x x 0 1 0 0 0 0 1 1 x x 0 0 0 0 0 0 0 1 x x 0 2 0 1 1 0 2 1 x x 0 0 0 0 0 0 0 1 x x 0 0 0 0 0 0 0 1 x x 
*/

/* Test case T09:
reset Coin clock Open Change 1 0 0 x x 1 0 1 x x 0 1 0 0 0 0 1 1 x x 0 1 0 0 0 0 1 1 x x 0 3 0 1 8 0 3 1 x x 0 0 0 0 0 0 0 1 x x 0 0 0 0 0 0 0 1 x x 
*/

/* Test case T07:
reset Coin clock Open Change 1 0 0 x x 1 0 1 x x 0 1 0 0 0 0 1 1 x x 0 1 0 0 0 0 1 1 x x 0 1 0 1 0 0 1 1 x x 0 0 0 0 0 0 0 1 x x 0 0 0 0 0 0 0 1 x x 
*/

/* Test case T05:
reset Coin clock Open Change 1 0 0 x x 1 0 1 x x 0 1 0 0 0 0 1 1 x x 0 2 0 1 1 0 2 1 x x 0 0 0 0 0 0 0 1 x x 0 0 0 0 0 0 0 1 x x 
*/

/* Test case T02:
reset Coin clock Open Change 1 0 0 x x 1 0 1 x x 0 2 0 0 0 0 2 1 x x 0 1 0 1 1 0 1 1 x x 0 0 0 0 0 0 0 1 x x 0 0 0 0 0 0 0 1 x x 
*/

/* Test case T01:
reset Coin clock Open Change 1 0 0 x x 1 0 1 x x 0 3 0 1 4 0 3 1 x x 0 0 0 0 0 0 0 1 x x 0 0 0 0 0 0 0 1 x x 
*/
