// Digital circuit act6_4.dig as structural Verilog
module act6_4 (
  input  reset,
  input  [1:0] Coin,
  input  clock,
  output Open,
  output [3:0] Change,
  output [3:0] S
);

  wire and_6_out, and_7_out, and_8_out, and_12_out, and_13_out, and_14_out, and_15_out, and_16_out,
       and_21_out, c2_or_c10, coin_0, coin_2, coin_5, coin_10, d0, d1, d2, d3, en, n_open, n_rst, nc0, nc1,
       ns1, ns2, or_2_out, or_3_out, or_4_out, or_5_out, or_6_out, or_7_out, or_8_out, or_9_out, t_d1_c5,
       t_d2_mid, xor_1_out, xor_2_out;

  and and_1 (en, n_rst, n_open);
  and and_2 (coin_0, nc1, nc0);
  and and_3 (coin_2, nc1, Coin[0]);
  and and_4 (coin_5, Coin[1], nc0);
  and and_5 (coin_10, Coin[1], Coin[0]);
  or or_1 (c2_or_c10, coin_2, coin_10);
  and and_6 (and_6_out, S[3], S[2]);
  xor xor_1 (xor_1_out, S[2], S[1]);
  and and_7 (and_7_out, ns2, S[0]);
  and and_8 (and_8_out, S[2], ns1);
  and and_9 (Change[0], Open, S[0]);
  not not_1 (n_rst, reset);
  not not_2 (nc1, Coin[1]);
  not not_3 (nc0, Coin[0]);
  not not_4 (ns2, S[2]);
  not not_5 (ns1, S[1]);
  not not_6 (n_open, Open);
  and and_10 (Change[3], and_6_out, S[1]);
  and and_11 (Change[2], xor_1_out, S[3]);
  or or_2 (or_2_out, and_7_out, and_8_out);
  and and_12 (and_12_out, coin_5, S[2]);
  or or_3 (or_3_out, S[1], S[2]);
  and and_13 (and_13_out, coin_0, S[2]);
  and and_14 (and_14_out, coin_5, ns2);
  or or_4 (or_4_out, S[1], S[0]);
  and and_15 (and_15_out, coin_0, S[1]);
  and and_16 (and_16_out, c2_or_c10, ns1);
  xor xor_2 (xor_2_out, coin_5, S[0]);
  and and_17 (Change[1], or_2_out, S[3]);
  or or_5 (or_5_out, and_12_out, coin_10);
  and and_18 (t_d2_mid, or_3_out, c2_or_c10);
  or or_6 (or_6_out, and_13_out, and_14_out);
  and and_19 (t_d1_c5, or_4_out, coin_5);
  or or_7 (or_7_out, and_15_out, and_16_out);
  and and_20 (d0, xor_2_out, en);
  and and_21 (and_21_out, S[2], S[1]);
  and and_22 (d3, or_5_out, en);
  or or_8 (or_8_out, or_6_out, t_d2_mid);
  or or_9 (or_9_out, or_7_out, t_d1_c5);
  or or_10 (Open, and_21_out, S[3]);
  and and_23 (d2, or_8_out, en);
  and and_24 (d1, or_9_out, en);
  D_FF d_ff_1 (.D(d3), .C(clock), .Q(S[3]));  // open: nQ
  D_FF d_ff_2 (.D(d2), .C(clock), .Q(S[2]));  // open: nQ
  D_FF d_ff_3 (.D(d1), .C(clock), .Q(S[1]));  // open: nQ
  D_FF d_ff_4 (.D(d0), .C(clock), .Q(S[0]));  // open: nQ

  // Other names for the same wires on the sheet: ch0 = Change[0]; ch1 = Change[1]; ch2 = Change[2]; ch3 = Change[3];
  //   clk = clock; c0 = Coin[0]; c1 = Coin[1]; open_out = Open
endmodule

/* Test case T14:
reset Coin clock Open Change S 1 0 0 x x x 1 0 1 0 0 0 1 0 0 x x x 1 0 1 0 0 0 1 0 0 x x x 1 0 1 0 0 0 1 0 0 x x x 1 0 1 0 0 0 0 0 0 0 0 0 0 0 1 0 0 0 0 0 0 0 0 0 0 0 1 0 0 0 0 0 0 0 0 0 0 0 1 0 0 0 0 0 0 0 0 0 0 0 1 0 0 0 0 0 0 0 0 0 0 0 1 0 0 0 0 0 0 0 0 0 0 0 1 0 0 0 0 1 0 0 0 0 0 1 1 0 0 2 0 1 0 0 0 2 0 1 1 0 0 4 0 2 0 0 0 4 0 2 1 1 3 9 0 0 0 1 3 9 0 0 1 0 0 0 0 0 0 0 0 0 0 0 1 0 0 0 0 0 0 0 0 0 0 0 1 0 0 0 0 0 0 0 0 0 0 0 1 0 0 0 1 0 0 x x x 1 0 1 0 0 0 1 0 0 x x x 1 0 1 0 0 0 0 0 0 0 0 0 0 0 1 0 0 0 0 0 0 0 0 0 0 0 1 0 0 0 0 2 0 0 0 0 0 2 1 0 0 5 0 3 0 0 0 5 0 3 1 1 9 15 0 0 0 1 9 15 0 0 1 0 0 0 
*/

/* Test case T12:
reset Coin clock Open Change S 1 0 0 x x x 1 0 1 0 0 0 0 1 0 0 0 0 0 1 1 0 0 2 1 0 0 x x x 1 0 1 0 0 0 0 0 0 0 0 0 0 0 1 0 0 0 0 1 0 0 0 0 0 1 1 0 0 2 0 1 0 0 0 2 0 1 1 0 0 4 1 0 0 x x x 1 0 1 0 0 0 0 0 0 0 0 0 0 0 1 0 0 0 0 2 0 0 0 0 0 2 1 0 0 5 1 0 0 x x x 1 0 1 0 0 0 0 0 0 0 0 0 0 0 1 0 0 0 0 1 0 0 0 0 0 1 1 0 0 2 0 1 0 0 0 2 0 1 1 0 0 4 0 1 0 0 0 4 0 1 1 1 0 6 0 0 0 1 0 6 0 0 1 0 0 0 0 2 0 0 0 0 0 2 1 0 0 5 0 0 0 0 0 5 0 0 1 0 0 5 1 0 0 x x x 1 0 1 0 0 0 0 3 0 0 0 0 0 3 1 1 4 10 0 0 0 1 4 10 0 0 1 0 0 0 
*/

/* Test case T10:
reset Coin clock Open Change S 1 0 0 x x x 1 0 1 0 0 0 0 0 0 0 0 0 0 0 1 0 0 0 0 0 0 0 0 0 0 0 1 0 0 0 0 1 0 0 0 0 0 1 1 0 0 2 0 0 0 0 0 2 0 0 1 0 0 2 0 0 0 0 0 2 0 0 1 0 0 2 0 1 0 0 0 2 0 1 1 0 0 4 0 0 0 0 0 4 0 0 1 0 0 4 0 0 0 0 0 4 0 0 1 0 0 4 0 0 0 0 0 4 0 0 1 0 0 4 0 2 0 0 0 4 0 2 1 1 3 9 0 0 0 1 3 9 0 0 1 0 0 0 0 0 0 0 0 0 0 0 1 0 0 0 0 2 0 0 0 0 0 2 1 0 0 5 0 0 0 0 0 5 0 0 1 0 0 5 0 0 0 0 0 5 0 0 1 0 0 5 0 3 0 0 0 5 0 3 1 1 9 15 0 0 0 1 9 15 0 0 1 0 0 0 0 1 0 0 0 0 0 1 1 0 0 2 0 0 0 0 0 2 0 0 1 0 0 2 0 2 0 0 0 2 0 2 1 1 1 7 0 0 0 1 1 7 0 0 1 0 0 0 0 0 0 0 0 0 0 0 1 0 0 0 
*/

/* Test case T09:
reset Coin clock Open Change S 1 0 0 x x x 1 0 1 0 0 0 0 1 0 0 0 0 0 1 1 0 0 2 0 1 0 0 0 2 0 1 1 0 0 4 0 3 0 0 0 4 0 3 1 1 8 14 0 0 0 1 8 14 0 0 1 0 0 0 0 0 0 0 0 0 0 0 1 0 0 0 
*/

/* Test case T07:
reset Coin clock Open Change S 1 0 0 x x x 1 0 1 0 0 0 0 1 0 0 0 0 0 1 1 0 0 2 0 1 0 0 0 2 0 1 1 0 0 4 0 1 0 0 0 4 0 1 1 1 0 6 0 0 0 1 0 6 0 0 1 0 0 0 0 0 0 0 0 0 0 0 1 0 0 0 
*/

/* Test case T05:
reset Coin clock Open Change S 1 0 0 x x x 1 0 1 0 0 0 0 1 0 0 0 0 0 1 1 0 0 2 0 2 0 0 0 2 0 2 1 1 1 7 0 0 0 1 1 7 0 0 1 0 0 0 0 0 0 0 0 0 0 0 1 0 0 0 
*/

/* Test case T02:
reset Coin clock Open Change S 1 0 0 x x x 1 0 1 0 0 0 0 2 0 0 0 0 0 2 1 0 0 5 0 1 0 0 0 5 0 1 1 1 1 7 0 0 0 1 1 7 0 0 1 0 0 0 0 0 0 0 0 0 0 0 1 0 0 0 
*/

/* Test case T01:
reset Coin clock Open Change S 1 0 0 x x x 1 0 1 0 0 0 0 3 0 0 0 0 0 3 1 1 4 10 0 0 0 1 4 10 0 0 1 0 0 0 0 0 0 0 0 0 0 0 1 0 0 0 
*/
