// Digital circuit act7_1.dig as structural Verilog
module act7_1 (
  input  [7:0] A,
  input  [7:0] B,
  input  start,
  input  reset,
  input  clock,
  output [7:0] gcd,
  output busy
);

  wire and_1_out, and_6_out, and_7_out, and_8_out, and_10_out, calc_sub, D0, D1, en_gcd, en_X, en_Y, load_st,
       multiplexer_7_out, not_eq, not_gt, not_reset, not_S0, not_S1, or_4_out, S0, S1, step_X, step_Y,
       X_eq_Y, X_gt_Y;
  wire [7:0] diff_XY, diff_YX, multiplexer_1_out, multiplexer_2_out, multiplexer_3_out, multiplexer_4_out,
       multiplexer_5_out, multiplexer_6_out, X, Y;

  Multiplexer #(.Bits(8)) multiplexer_1 (.sel(not_S0), .in_0(diff_XY), .in_1(A), .out(multiplexer_1_out));
  Multiplexer #(.Bits(8)) multiplexer_2 (.sel(not_S0), .in_0(diff_YX), .in_1(B), .out(multiplexer_2_out));
  Multiplexer #(.Bits(8)) multiplexer_3 (.sel(reset), .in_0(X), .in_1({8{1'b0}}), .out(multiplexer_3_out));
  and and_1 (and_1_out, not_S1, not_S0);
  and and_2 (calc_sub, busy, not_eq);
  and and_3 (step_Y, calc_sub, not_gt);
  Multiplexer #(.Bits(8)) multiplexer_4 (.sel(en_X), .in_0(X), .in_1(multiplexer_1_out), .out(multiplexer_4_out));
  Multiplexer #(.Bits(8)) multiplexer_5 (.sel(en_Y), .in_0(Y), .in_1(multiplexer_2_out), .out(multiplexer_5_out));
  Multiplexer #(.Bits(8)) multiplexer_6 (.sel(en_gcd), .in_0(gcd), .in_1(multiplexer_3_out), .out(multiplexer_6_out));
  and and_4 (load_st, and_1_out, start);
  and and_5 (step_X, calc_sub, X_gt_Y);
  or or_1 (en_Y, load_st, step_Y);
  D_FF #(.Bits(8)) d_ff_1 (.D(multiplexer_4_out), .C(clock), .Q(X));  // open: nQ
  D_FF #(.Bits(8)) d_ff_2 (.D(multiplexer_5_out), .C(clock), .Q(Y));  // open: nQ
  D_FF #(.Bits(8)) d_ff_3 (.D(multiplexer_6_out), .C(clock), .Q(gcd));  // open: nQ
  or or_2 (en_X, load_st, step_X);
  Sub #(.Bits(8)) sub_1 (.a(X), .b(Y), .c_i(1'b0), .s(diff_XY));  // open: c_o
  Sub #(.Bits(8)) sub_2 (.a(Y), .b(X), .c_i(1'b0), .s(diff_YX));  // open: c_o
  Comparator #(.Bits(8)) comparator_1 (.a(X), .b(Y), .gt(X_gt_Y), .eq(X_eq_Y));  // open: lt
  and and_6 (and_6_out, busy, X_eq_Y);
  Multiplexer multiplexer_7 (.sel(S0), .in_0(start), .in_1(not_eq), .out(multiplexer_7_out));
  and and_7 (and_7_out, S0, X_eq_Y);
  or or_3 (en_gcd, and_6_out, reset);
  D_FF d_ff_4 (.D(D0), .C(clock), .Q(S0), .nQ(not_S0));
  D_FF d_ff_5 (.D(D1), .C(clock), .Q(S1), .nQ(not_S1));
  and and_8 (and_8_out, multiplexer_7_out, not_S1);
  or or_4 (or_4_out, S1, and_7_out);
  and and_9 (D0, and_8_out, not_reset);
  and and_10 (and_10_out, or_4_out, start);
  and and_11 (D1, and_10_out, not_reset);
  and and_12 (busy, not_S1, S0);
  not not_1 (not_reset, reset);
  not not_2 (not_eq, X_eq_Y);
  not not_3 (not_gt, X_gt_Y);

  // Other names for the same wires on the sheet: busy_out = busy; gcd_out[7:0] = gcd
endmodule

/* Test case T11:
A B start reset clock gcd busy 0 0 0 1 0 x x 0 0 0 1 1 0 0 255 1 1 0 0 x x 255 1 1 0 1 x 1 repeat(20) 255 1 0 0 C x x 255 1 0 1 0 x x 255 1 0 1 1 0 0 255 1 0 0 0 0 0 255 1 0 0 1 0 0 255 1 0 0 0 0 0 255 1 0 0 1 0 0 255 1 0 0 0 0 0 255 1 0 0 1 0 0 18 24 1 0 0 x x 18 24 1 0 1 x 1 repeat(600) 18 24 0 0 C x x 18 24 0 0 0 6 0 18 24 0 0 1 6 0 18 24 0 0 0 6 0 18 24 0 0 1 6 0 18 24 0 1 0 x x 18 24 0 1 1 0 0 18 24 0 1 0 x x 18 24 0 1 1 0 0 18 24 0 0 0 0 0 18 24 0 0 1 0 0 18 24 0 0 0 0 0 18 24 0 0 1 0 0 100 75 1 0 0 x x 100 75 1 0 1 x 1 repeat(600) 100 75 0 0 C x x 100 75 0 0 0 25 0 100 75 0 0 1 25 0 100 75 0 0 0 25 0 100 75 0 0 1 25 0 
*/

/* Test case T09:
A B start reset clock gcd busy 0 0 0 1 0 x x 0 0 0 1 1 0 0 84 36 1 0 0 x x 84 36 1 0 1 x 1 repeat(600) 84 36 0 0 C x x 84 36 0 0 0 12 0 84 36 0 0 1 12 0 10 3 0 0 0 12 0 10 3 0 0 1 12 0 10 3 0 0 0 12 0 10 3 0 0 1 12 0 10 3 0 0 0 12 0 10 3 0 0 1 12 0 10 3 0 0 0 12 0 10 3 0 0 1 12 0 10 3 0 0 0 12 0 10 3 0 0 1 12 0 10 3 0 0 0 12 0 10 3 0 0 1 12 0 45 60 1 0 0 x x 45 60 1 0 1 x 1 repeat(600) 45 60 0 0 C x x 45 60 0 0 0 15 0 45 60 0 0 1 15 0 99 1 0 0 0 15 0 99 1 0 0 1 15 0 99 1 0 0 0 15 0 99 1 0 0 1 15 0 99 1 0 0 0 15 0 99 1 0 0 1 15 0 99 1 0 0 0 15 0 99 1 0 0 1 15 0 99 1 0 0 0 15 0 99 1 0 0 1 15 0 99 1 0 0 0 15 0 99 1 0 0 1 15 0 121 11 1 0 0 x x 121 11 1 0 1 x 1 repeat(600) 121 11 0 0 C x x 121 11 0 0 0 11 0 121 11 0 0 1 11 0 7 7 0 0 0 11 0 7 7 0 0 1 11 0 7 7 0 0 0 11 0 7 7 0 0 1 11 0 7 7 0 0 0 11 0 7 7 0 0 1 11 0 7 7 0 0 0 11 0 7 7 0 0 1 11 0 7 7 0 0 0 11 0 7 7 0 0 1 11 0 7 7 0 0 0 11 0 7 7 0 0 1 11 0 
*/

/* Test case T07:
A B start reset clock gcd busy 0 0 0 1 0 x x 0 0 0 1 1 0 0 255 1 1 0 0 x x 255 1 1 0 1 x 1 repeat(600) 255 1 0 0 C x x 255 1 0 0 0 1 0 255 1 0 0 1 1 0 255 1 0 0 0 1 0 255 1 0 0 1 1 0 1 255 1 0 0 x x 1 255 1 0 1 x 1 repeat(600) 1 255 0 0 C x x 1 255 0 0 0 1 0 1 255 0 0 1 1 0 1 255 0 0 0 1 0 1 255 0 0 1 1 0 255 254 1 0 0 x x 255 254 1 0 1 x 1 repeat(600) 255 254 0 0 C x x 255 254 0 0 0 1 0 255 254 0 0 1 1 0 255 254 0 0 0 1 0 255 254 0 0 1 1 0 254 255 1 0 0 x x 254 255 1 0 1 x 1 repeat(600) 254 255 0 0 C x x 254 255 0 0 0 1 0 254 255 0 0 1 1 0 254 255 0 0 0 1 0 254 255 0 0 1 1 0 
*/

/* Test case T06:
A B start reset clock gcd busy 0 0 0 1 0 x x 0 0 0 1 1 0 0 1 200 1 0 0 x x 1 200 1 0 1 x 1 repeat(600) 1 200 0 0 C x x 1 200 0 0 0 1 0 1 200 0 0 1 1 0 1 200 0 0 0 1 0 1 200 0 0 1 1 0 200 1 1 0 0 x x 200 1 1 0 1 x 1 repeat(600) 200 1 0 0 C x x 200 1 0 0 0 1 0 200 1 0 0 1 1 0 200 1 0 0 0 1 0 200 1 0 0 1 1 0 2 1 1 0 0 x x 2 1 1 0 1 x 1 repeat(600) 2 1 0 0 C x x 2 1 0 0 0 1 0 2 1 0 0 1 1 0 2 1 0 0 0 1 0 2 1 0 0 1 1 0 
*/

/* Test case T05:
A B start reset clock gcd busy 0 0 0 1 0 x x 0 0 0 1 1 0 0 84 36 1 0 0 x x 84 36 1 0 1 x 1 repeat(600) 84 36 0 0 C x x 84 36 0 0 0 12 0 84 36 0 0 1 12 0 84 36 0 0 0 12 0 84 36 0 0 1 12 0 36 84 1 0 0 x x 36 84 1 0 1 x 1 repeat(600) 36 84 0 0 C x x 36 84 0 0 0 12 0 36 84 0 0 1 12 0 36 84 0 0 0 12 0 36 84 0 0 1 12 0 120 75 1 0 0 x x 120 75 1 0 1 x 1 repeat(600) 120 75 0 0 C x x 120 75 0 0 0 15 0 120 75 0 0 1 15 0 120 75 0 0 0 15 0 120 75 0 0 1 15 0 
*/

/* Test case T02:
A B start reset clock gcd busy 0 0 0 1 0 x x 0 0 0 1 1 0 0 48 12 1 0 0 x x 48 12 1 0 1 x 1 repeat(600) 48 12 0 0 C x x 48 12 0 0 0 12 0 48 12 0 0 1 12 0 48 12 0 0 0 12 0 48 12 0 0 1 12 0 255 5 1 0 0 x x 255 5 1 0 1 x 1 repeat(600) 255 5 0 0 C x x 255 5 0 0 0 5 0 255 5 0 0 1 5 0 255 5 0 0 0 5 0 255 5 0 0 1 5 0 128 2 1 0 0 x x 128 2 1 0 1 x 1 repeat(600) 128 2 0 0 C x x 128 2 0 0 0 2 0 128 2 0 0 1 2 0 128 2 0 0 0 2 0 128 2 0 0 1 2 0 
*/

/* Test case T01:
A B start reset clock gcd busy 0 0 0 1 0 x x 0 0 0 1 1 0 0 12 12 1 0 0 x x 12 12 1 0 1 x 1 repeat(600) 12 12 0 0 C x x 12 12 0 0 0 12 0 12 12 0 0 1 12 0 12 12 0 0 0 12 0 12 12 0 0 1 12 0 200 200 1 0 0 x x 200 200 1 0 1 x 1 repeat(600) 200 200 0 0 C x x 200 200 0 0 0 200 0 200 200 0 0 1 200 0 200 200 0 0 0 200 0 200 200 0 0 1 200 0 1 1 1 0 0 x x 1 1 1 0 1 x 1 repeat(600) 1 1 0 0 C x x 1 1 0 0 0 1 0 1 1 0 0 1 1 0 1 1 0 0 0 1 0 1 1 0 0 1 1 0 
*/
