// Digital circuit act7_2.dig as structural Verilog
module act7_2 (
  input  [7:0] N,
  input  \new ,
  input  reset,
  input  clock,
  output [7:0] num_inc,
  output [7:0] max,
  output busy
);

  wire and_1_out, and_5_out, and_8_out, and_9_out, busy_keep, can_start, done, has_first, is_greater, n_busy,
       n_done, n_new_prev, n_rst, new_prev, new_rise, not_has_first, or_1_out, or_2_out, or_3_out,
       start_calc, take_N;
  wire [7:0] multiplexer_1_out, multiplexer_2_out, multiplexer_3_out, multiplexer_4_out, multiplexer_5_out,
       multiplexer_6_out, multiplexer_7_out, multiplexer_8_out, N_latched, num_plus_1;

  not not_1 (n_rst, reset);
  not not_2 (n_busy, busy);
  not not_3 (n_done, done);
  not not_4 (not_has_first, has_first);
  and and_1 (and_1_out, \new , n_rst);
  and and_2 (new_rise, \new , n_new_prev);
  and and_3 (can_start, n_busy, n_rst);
  and and_4 (busy_keep, busy, n_done);
  or or_1 (or_1_out, has_first, done);
  or or_2 (or_2_out, not_has_first, is_greater);
  Multiplexer #(.Bits(8)) multiplexer_1 (.sel(is_greater), .in_0(num_inc), .in_1(num_plus_1), .out(multiplexer_1_out));
  D_FF d_ff_1 (.D(and_1_out), .C(clock), .Q(new_prev));  // open: nQ
  and and_5 (and_5_out, or_1_out, n_rst);
  and and_6 (take_N, or_2_out, done);
  not not_5 (n_new_prev, new_prev);
  or or_3 (or_3_out, start_calc, busy_keep);
  Multiplexer #(.Bits(8)) multiplexer_2 (
    .sel(not_has_first), .in_0(multiplexer_1_out), .in_1(8'h1), .out(multiplexer_2_out));
  D_FF d_ff_2 (.D(and_5_out), .C(clock), .Q(has_first));  // open: nQ
  and and_7 (start_calc, new_rise, can_start);
  and and_8 (and_8_out, or_3_out, n_rst);
  Multiplexer #(.Bits(8)) multiplexer_3 (.sel(done), .in_0(num_inc), .in_1(multiplexer_2_out), .out(multiplexer_3_out));
  D_FF d_ff_3 (.D(and_8_out), .C(clock), .Q(busy));  // open: nQ
  Multiplexer #(.Bits(8)) multiplexer_4 (.sel(take_N), .in_0(max), .in_1(N_latched), .out(multiplexer_4_out));
  Multiplexer #(.Bits(8)) multiplexer_5 (
    .sel(reset), .in_0(multiplexer_3_out), .in_1({8{1'b0}}), .out(multiplexer_5_out));
  Multiplexer #(.Bits(8)) multiplexer_6 (.sel(start_calc), .in_0(N_latched), .in_1(N), .out(multiplexer_6_out));
  Multiplexer #(.Bits(8)) multiplexer_7 (
    .sel(reset), .in_0(multiplexer_4_out), .in_1({8{1'b0}}), .out(multiplexer_7_out));
  D_FF #(.Bits(8)) d_ff_4 (.D(multiplexer_5_out), .C(clock), .Q(num_inc));  // open: nQ
  Multiplexer #(.Bits(8)) multiplexer_8 (
    .sel(reset), .in_0(multiplexer_6_out), .in_1({8{1'b0}}), .out(multiplexer_8_out));
  D_FF #(.Bits(8)) d_ff_5 (.D(multiplexer_7_out), .C(clock), .Q(max));  // open: nQ
  D_FF #(.Bits(8)) d_ff_6 (.D(multiplexer_8_out), .C(clock), .Q(N_latched));  // open: nQ
  and and_9 (and_9_out, start_calc, n_rst);
  D_FF d_ff_7 (.D(and_9_out), .C(clock), .Q(done));  // open: nQ
  Comparator #(.Bits(8)) comparator_1 (.a(N_latched), .b(max), .gt(is_greater));  // open: eq, lt
  Add #(.Bits(8)) add_1 (.a(num_inc), .b(8'h1), .c_i(1'b0), .s(num_plus_1));  // open: c_o

  // Other names for the same wires on the sheet: busy_out = busy; clk = clock; max_out[7:0] = max; N_in[7:0] = N;
  //   new_in = \new ; num_inc_out[7:0] = num_inc; reset_in = reset
endmodule

/* Test case T10:
N new reset clock num_inc max busy 0 0 1 0 x x x 0 0 1 1 0 0 0 20 1 0 0 x x x 20 1 0 1 x x 1 90 1 0 0 x x x 90 1 0 1 x x x 90 1 0 0 x x x 90 1 0 1 x x x 90 1 0 0 x x x 90 1 0 1 x x x 90 1 0 0 x x x 90 1 0 1 x x x 0 0 0 0 x x x 0 0 0 1 x x x 0 0 0 0 x x x 0 0 0 1 x x x 0 0 0 0 x x x 0 0 0 1 x x x 0 0 0 0 x x x 0 0 0 1 x x x 0 0 0 0 x x x 0 0 0 1 x x x 0 0 0 0 x x x 0 0 0 1 x x x 0 0 0 0 x x x 0 0 0 1 x x x 0 0 0 0 x x x 0 0 0 1 x x x 0 0 0 0 x x x 0 0 0 1 x x x 0 0 0 0 x x x 0 0 0 1 x x x 0 0 0 0 x x x 0 0 0 1 x x x 0 0 0 0 x x x 0 0 0 1 x x x 0 0 0 0 x x x 0 0 0 1 x x x 0 0 0 0 x x x 0 0 0 1 x x x 0 0 0 0 x x x 0 0 0 1 x x x 0 0 0 0 x x x 0 0 0 1 x x x 0 0 0 0 x x x 0 0 0 1 x x x 0 0 0 0 x x x 0 0 0 1 x x x 0 0 0 0 x x x 0 0 0 1 x x x 0 0 0 0 x x x 0 0 0 1 x x x 0 0 0 0 x x x 0 0 0 1 x x x 0 0 0 0 x x x 0 0 0 1 x x x 0 0 0 0 x x x 0 0 0 1 x x x 0 0 0 0 x x x 0 0 0 1 x x x 0 0 0 0 x x x 0 0 0 1 x x x 0 0 0 0 x x x 0 0 0 1 x x x 0 0 0 0 1 20 0 0 0 0 1 1 20 0 50 1 0 0 x x x 50 1 0 1 x x 1 200 1 0 0 x x x 200 1 0 1 x x x 200 1 0 0 x x x 200 1 0 1 x x x 200 1 0 0 x x x 200 1 0 1 x x x 200 1 0 0 x x x 200 1 0 1 x x x 0 0 0 0 x x x 0 0 0 1 x x x 0 0 0 0 x x x 0 0 0 1 x x x 0 0 0 0 x x x 0 0 0 1 x x x 0 0 0 0 x x x 0 0 0 1 x x x 0 0 0 0 x x x 0 0 0 1 x x x 0 0 0 0 x x x 0 0 0 1 x x x 0 0 0 0 x x x 0 0 0 1 x x x 0 0 0 0 x x x 0 0 0 1 x x x 0 0 0 0 x x x 0 0 0 1 x x x 0 0 0 0 x x x 0 0 0 1 x x x 0 0 0 0 x x x 0 0 0 1 x x x 0 0 0 0 x x x 0 0 0 1 x x x 0 0 0 0 x x x 0 0 0 1 x x x 0 0 0 0 x x x 0 0 0 1 x x x 0 0 0 0 x x x 0 0 0 1 x x x 0 0 0 0 x x x 0 0 0 1 x x x 0 0 0 0 x x x 0 0 0 1 x x x 0 0 0 0 x x x 0 0 0 1 x x x 0 0 0 0 x x x 0 0 0 1 x x x 0 0 0 0 x x x 0 0 0 1 x x x 0 0 0 0 x x x 0 0 0 1 x x x 0 0 0 0 x x x 0 0 0 1 x x x 0 0 0 0 x x x 0 0 0 1 x x x 0 0 0 0 x x x 0 0 0 1 x x x 0 0 0 0 x x x 0 0 0 1 x x x 0 0 0 0 x x x 0 0 0 1 x x x 0 0 0 0 2 50 0 0 0 0 1 2 50 0 60 1 0 0 x x x 60 1 0 1 x x 1 70 1 0 0 x x x 70 1 0 1 x x x 70 1 0 0 x x x 70 1 0 1 x x x 70 1 0 0 x x x 70 1 0 1 x x x 70 1 0 0 x x x 70 1 0 1 x x x 0 0 0 0 x x x 0 0 0 1 x x x 0 0 0 0 x x x 0 0 0 1 x x x 0 0 0 0 x x x 0 0 0 1 x x x 0 0 0 0 x x x 0 0 0 1 x x x 0 0 0 0 x x x 0 0 0 1 x x x 0 0 0 0 x x x 0 0 0 1 x x x 0 0 0 0 x x x 0 0 0 1 x x x 0 0 0 0 x x x 0 0 0 1 x x x 0 0 0 0 x x x 0 0 0 1 x x x 0 0 0 0 x x x 0 0 0 1 x x x 0 0 0 0 x x x 0 0 0 1 x x x 0 0 0 0 x x x 0 0 0 1 x x x 0 0 0 0 x x x 0 0 0 1 x x x 0 0 0 0 x x x 0 0 0 1 x x x 0 0 0 0 x x x 0 0 0 1 x x x 0 0 0 0 x x x 0 0 0 1 x x x 0 0 0 0 x x x 0 0 0 1 x x x 0 0 0 0 x x x 0 0 0 1 x x x 0 0 0 0 x x x 0 0 0 1 x x x 0 0 0 0 x x x 0 0 0 1 x x x 0 0 0 0 x x x 0 0 0 1 x x x 0 0 0 0 x x x 0 0 0 1 x x x 0 0 0 0 x x x 0 0 0 1 x x x 0 0 0 0 x x x 0 0 0 1 x x x 0 0 0 0 x x x 0 0 0 1 x x x 0 0 0 0 x x x 0 0 0 1 x x x 0 0 0 0 3 60 0 0 0 0 1 3 60 0 10 1 0 0 x x x 10 1 0 1 x x 1 250 1 0 0 x x x 250 1 0 1 x x x 250 1 0 0 x x x 250 1 0 1 x x x 250 1 0 0 x x x 250 1 0 1 x x x 250 1 0 0 x x x 250 1 0 1 x x x 0 0 0 0 x x x 0 0 0 1 x x x 0 0 0 0 x x x 0 0 0 1 x x x 0 0 0 0 x x x 0 0 0 1 x x x 0 0 0 0 x x x 0 0 0 1 x x x 0 0 0 0 x x x 0 0 0 1 x x x 0 0 0 0 x x x 0 0 0 1 x x x 0 0 0 0 x x x 0 0 0 1 x x x 0 0 0 0 x x x 0 0 0 1 x x x 0 0 0 0 x x x 0 0 0 1 x x x 0 0 0 0 x x x 0 0 0 1 x x x 0 0 0 0 x x x 0 0 0 1 x x x 0 0 0 0 x x x 0 0 0 1 x x x 0 0 0 0 x x x 0 0 0 1 x x x 0 0 0 0 x x x 0 0 0 1 x x x 0 0 0 0 x x x 0 0 0 1 x x x 0 0 0 0 x x x 0 0 0 1 x x x 0 0 0 0 x x x 0 0 0 1 x x x 0 0 0 0 x x x 0 0 0 1 x x x 0 0 0 0 x x x 0 0 0 1 x x x 0 0 0 0 x x x 0 0 0 1 x x x 0 0 0 0 x x x 0 0 0 1 x x x 0 0 0 0 x x x 0 0 0 1 x x x 0 0 0 0 x x x 0 0 0 1 x x x 0 0 0 0 x x x 0 0 0 1 x x x 0 0 0 0 x x x 0 0 0 1 x x x 0 0 0 0 x x x 0 0 0 1 x x x 0 0 0 0 3 60 0 0 0 0 1 3 60 0 100 1 0 0 x x x 100 1 0 1 x x 1 255 1 0 0 x x x 255 1 0 1 x x x 255 1 0 0 x x x 255 1 0 1 x x x 255 1 0 0 x x x 255 1 0 1 x x x 255 1 0 0 x x x 255 1 0 1 x x x 0 0 0 0 x x x 0 0 0 1 x x x 0 0 0 0 x x x 0 0 0 1 x x x 0 0 0 0 x x x 0 0 0 1 x x x 0 0 0 0 x x x 0 0 0 1 x x x 0 0 0 0 x x x 0 0
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*/

/* Test case T06:
N new reset clock num_inc max busy 0 0 1 0 x x x 0 0 1 1 0 0 0 131 1 0 0 x x x 131 1 0 1 x x 1 0 0 0 0 x x x 0 0 0 1 x x x 0 0 0 0 x x x 0 0 0 1 x x x 0 0 0 0 x x x 0 0 0 1 x x x 0 0 0 0 x x x 0 0 0 1 x x x 0 0 0 0 x x x 0 0 0 1 x x x 0 0 0 0 x x x 0 0 0 1 x x x 0 0 0 0 x x x 0 0 0 1 x x x 0 0 0 0 x x x 0 0 0 1 x x x 0 0 0 0 x x x 0 0 0 1 x x x 0 0 0 0 x x x 0 0 0 1 x x x 0 0 0 0 x x x 0 0 0 1 x x x 0 0 0 0 x x x 0 0 0 1 x x x 0 0 0 0 x x x 0 0 0 1 x x x 0 0 0 0 x x x 0 0 0 1 x x x 0 0 0 0 x x x 0 0 0 1 x x x 0 0 0 0 x x x 0 0 0 1 x x x 0 0 0 0 x x x 0 0 0 1 x x x 0 0 0 0 x x x 0 0 0 1 x x x 0 0 0 0 x x x 0 0 0 1 x x x 0 0 0 0 x x x 0 0 0 1 x x x 0 0 0 0 x x x 0 0 0 1 x x x 0 0 0 0 x x x 0 0 0 1 x x x 0 0 0 0 x x x 0 0 0 1 x x x 0 0 0 0 x x x 0 0 0 1 x x x 0 0 0 0 x x x 0 0 0 1 x x x 0 0 0 0 x x x 0 0 0 1 x x x 0 0 0 0 x x x 0 0 0 1 x x x 0 0 0 0 x x x 0 0 0 1 x x x 0 0 0 0 x x x 0 0 0 1 x x x 0 0 0 0 x x x 0 0 0 1 x x x 0 0 0 0 1 131 0 0 0 0 1 1 131 0 130 1 0 0 x x x 130 1 0 1 x x 1 0 0 0 0 x x x 0 0 0 1 x x x 0 0 0 0 x x x 0 0 0 1 x x x 0 0 0 0 x x x 0 0 0 1 x x x 0 0 0 0 x x x 0 0 0 1 x x x 0 0 0 0 x x x 0 0 0 1 x x x 0 0 0 0 x x x 0 0 0 1 x x x 0 0 0 0 x x x 0 0 0 1 x x x 0 0 0 0 x x x 0 0 0 1 x x x 0 0 0 0 x x x 0 0 0 1 x x x 0 0 0 0 x x x 0 0 0 1 x x x 0 0 0 0 x x x 0 0 0 1 x x x 0 0 0 0 x x x 0 0 0 1 x x x 0 0 0 0 x x x 0 0 0 1 x x x 0 0 0 0 x x x 0 0 0 1 x x x 0 0 0 0 x x x 0 0 0 1 x x x 0 0 0 0 x x x 0 0 0 1 x x x 0 0 0 0 x x x 0 0 0 1 x x x 0 0 0 0 x x x 0 0 0 1 x x x 0 0 0 0 x x x 0 0 0 1 x x x 0 0 0 0 x x x 0 0 0 1 x x x 0 0 0 0 x x x 0 0 0 1 x x x 0 0 0 0 x x x 0 0 0 1 x x x 0 0 0 0 x x x 0 0 0 1 x x x 0 0 0 0 x x x 0 0 0 1 x x x 0 0 0 0 x x x 0 0 0 1 x x x 0 0 0 0 x x x 0 0 0 1 x x x 0 0 0 0 x x x 0 0 0 1 x x x 0 0 0 0 x x x 0 0 0 1 x x x 0 0 0 0 x x x 0 0 0 1 x x x 0 0 0 0 x x x 0 0 0 1 x x x 0 0 0 0 1 131 0 0 0 0 1 1 131 0 58 1 0 0 x x x 58 1 0 1 x x 1 0 0 0 0 x x x 0 0 0 1 x x x 0 0 0 0 x x x 0 0 0 1 x x x 0 0 0 0 x x x 0 0 0 1 x x x 0 0 0 0 x x x 0 0 0 1 x x x 0 0 0 0 x x x 0 0 0 1 x x x 0 0 0 0 x x x 0 0 0 1 x x x 0 0 0 0 x x x 0 0 0 1 x x x 0 0 0 0 x x x 0 0 0 1 x x x 0 0 0 0 x x x 0 0 0 1 x x x 0 0 0 0 x x x 0 0 0 1 x x x 0 0 0 0 x x x 0 0 0 1 x x x 0 0 0 0 x x x 0 0 0 1 x x x 0 0 0 0 x x x 0 0 0 1 x x x 0 0 0 0 x x x 0 0 0 1 x x x 0 0 0 0 x x x 0 0 0 1 x x x 0 0 0 0 x x x 0 0 0 1 x x x 0 0 0 0 x x x 0 0 0 1 x x x 0 0 0 0 x x x 0 0 0 1 x x x 0 0 0 0 x x x 0 0 0 1 x x x 0 0 0 0 x x x 0 0 0 1 x x x 0 0 0 0 x x x 0 0 0 1 x x x 0 0 0 0 x x x 0 0 0 1 x x x 0 0 0 0 x x x 0 0 0 1 x x x 0 0 0 0 x x x 0 0 0 1 x x x 0 0 0 0 x x x 0 0 0 1 x x x 0 0 0 0 x x x 0 0 0 1 x x x 0 0 0 0 x x x 0 0 0 1 x x x 0 0 0 0 x x x 0 0 0 1 x x x 0 0 0 0 x x x 0 0 0 1 x x x 0 0 0 0 x x x 0 0 0 1 x x x 0 0 0 0 1 131 0 0 0 0 1 1 131 0 154 1 0 0 x x x 154 1 0 1 x x 1 0 0 0 0 x x x 0 0 0 1 x x x 0 0 0 0 x x x 0 0 0 1 x x x 0 0 0 0 x x x 0 0 0 1 x x x 0 0 0 0 x x x 0 0 0 1 x x x 0 0 0 0 x x x 0 0 0 1 x x x 0 0 0 0 x x x 0 0 0 1 x x x 0 0 0 0 x x x 0 0 0 1 x x x 0 0 0 0 x x x 0 0 0 1 x x x 0 0 0 0 x x x 0 0 0 1 x x x 0 0 0 0 x x x 0 0 0 1 x x x 0 0 0 0 x x x 0 0 0 1 x x x 0 0 0 0 x x x 0 0 0 1 x x x 0 0 0 0 x x x 0 0 0 1 x x x 0 0 0 0 x x x 0 0 0 1 x x x 0 0 0 0 x x x 0 0 0 1 x x x 0 0 0 0 x x x 0 0 0 1 x x x 0 0 0 0 x x x 0 0 0 1 x x x 0 0 0 0 x x x 0 0 0 1 x x x 0 0 0 0 x x x 0 0 0 1 x x x 0 0 0 0 x x x 0 0 0 1 x x x 0 0 0 0 x x x 0 0 0 1 x x x 0 0 0 0 x x x 0 0 0 1 x x x 0 0 0 0 x x x 0 0 0 1 x x x 0 0 0 0 x x x 0 0 0 1 x x x 0 0 0 0 x x x 0 0 0 1 x x x 0 0 0 0 x x x 0 0 0 1 x x x 0 0 0 0 x x x 0 0 0 1 x x x 0 0 0 0 x x x 0 0 0 1 x x x 0 0 0 0 x x x 0 0 0 1 x x x 0 0 0 0 x x x 0 0 0 1 x x x 0 0 0 0 2 154 0 0 0 0 1 2 154 0 122 1 0 0 x x x 122 1 0 1 x x 1 0 0 0 0 x x x 0 0 0 1 x x x 0 0 0 0 x x x 0 0 0 1 x x x 0 0 0 0 x x x 0 0 0 1 x x x 0 0 0 0 x x x 0 0 0 1 x x x 0 0 0 0 x x x 0 0 0 1 x x x 0 0 0 0 x x x 0 0 0 1 x x x 0 0 0 0 x x x 0 0 0 1 x x x 0 0 0 0 x x x 0 0 0 1 x x x 0 0 0 0 x x x 0 0 0 1 x x x 0 0 0 0 x x x 0 0 0 1 x x x 0 0 0 0 x x
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*/

/* Test case T03:
N new reset clock num_inc max busy 0 0 1 0 x x x 0 0 1 1 0 0 0 20 1 0 0 x x x 20 1 0 1 x x 1 0 0 0 0 x x x 0 0 0 1 x x x 0 0 0 0 x x x 0 0 0 1 x x x 0 0 0 0 x x x 0 0 0 1 x x x 0 0 0 0 x x x 0 0 0 1 x x x 0 0 0 0 x x x 0 0 0 1 x x x 0 0 0 0 x x x 0 0 0 1 x x x 0 0 0 0 x x x 0 0 0 1 x x x 0 0 0 0 x x x 0 0 0 1 x x x 0 0 0 0 x x x 0 0 0 1 x x x 0 0 0 0 x x x 0 0 0 1 x x x 0 0 0 0 x x x 0 0 0 1 x x x 0 0 0 0 x x x 0 0 0 1 x x x 0 0 0 0 x x x 0 0 0 1 x x x 0 0 0 0 x x x 0 0 0 1 x x x 0 0 0 0 x x x 0 0 0 1 x x x 0 0 0 0 x x x 0 0 0 1 x x x 0 0 0 0 x x x 0 0 0 1 x x x 0 0 0 0 x x x 0 0 0 1 x x x 0 0 0 0 x x x 0 0 0 1 x x x 0 0 0 0 x x x 0 0 0 1 x x x 0 0 0 0 x x x 0 0 0 1 x x x 0 0 0 0 x x x 0 0 0 1 x x x 0 0 0 0 x x x 0 0 0 1 x x x 0 0 0 0 x x x 0 0 0 1 x x x 0 0 0 0 x x x 0 0 0 1 x x x 0 0 0 0 x x x 0 0 0 1 x x x 0 0 0 0 x x x 0 0 0 1 x x x 0 0 0 0 x x x 0 0 0 1 x x x 0 0 0 0 x x x 0 0 0 1 x x x 0 0 0 0 x x x 0 0 0 1 x x x 0 0 0 0 1 20 0 0 0 0 1 1 20 0 14 1 0 0 x x x 14 1 0 1 x x 1 0 0 0 0 x x x 0 0 0 1 x x x 0 0 0 0 x x x 0 0 0 1 x x x 0 0 0 0 x x x 0 0 0 1 x x x 0 0 0 0 x x x 0 0 0 1 x x x 0 0 0 0 x x x 0 0 0 1 x x x 0 0 0 0 x x x 0 0 0 1 x x x 0 0 0 0 x x x 0 0 0 1 x x x 0 0 0 0 x x x 0 0 0 1 x x x 0 0 0 0 x x x 0 0 0 1 x x x 0 0 0 0 x x x 0 0 0 1 x x x 0 0 0 0 x x x 0 0 0 1 x x x 0 0 0 0 x x x 0 0 0 1 x x x 0 0 0 0 x x x 0 0 0 1 x x x 0 0 0 0 x x x 0 0 0 1 x x x 0 0 0 0 x x x 0 0 0 1 x x x 0 0 0 0 x x x 0 0 0 1 x x x 0 0 0 0 x x x 0 0 0 1 x x x 0 0 0 0 x x x 0 0 0 1 x x x 0 0 0 0 x x x 0 0 0 1 x x x 0 0 0 0 x x x 0 0 0 1 x x x 0 0 0 0 x x x 0 0 0 1 x x x 0 0 0 0 x x x 0 0 0 1 x x x 0 0 0 0 x x x 0 0 0 1 x x x 0 0 0 0 x x x 0 0 0 1 x x x 0 0 0 0 x x x 0 0 0 1 x x x 0 0 0 0 x x x 0 0 0 1 x x x 0 0 0 0 x x x 0 0 0 1 x x x 0 0 0 0 x x x 0 0 0 1 x x x 0 0 0 0 x x x 0 0 0 1 x x x 0 0 0 0 x x x 0 0 0 1 x x x 0 0 0 0 1 20 0 0 0 0 1 1 20 0 27 1 0 0 x x x 27 1 0 1 x x 1 0 0 0 0 x x x 0 0 0 1 x x x 0 0 0 0 x x x 0 0 0 1 x x x 0 0 0 0 x x x 0 0 0 1 x x x 0 0 0 0 x x x 0 0 0 1 x x x 0 0 0 0 x x x 0 0 0 1 x x x 0 0 0 0 x x x 0 0 0 1 x x x 0 0 0 0 x x x 0 0 0 1 x x x 0 0 0 0 x x x 0 0 0 1 x x x 0 0 0 0 x x x 0 0 0 1 x x x 0 0 0 0 x x x 0 0 0 1 x x x 0 0 0 0 x x x 0 0 0 1 x x x 0 0 0 0 x x x 0 0 0 1 x x x 0 0 0 0 x x x 0 0 0 1 x x x 0 0 0 0 x x x 0 0 0 1 x x x 0 0 0 0 x x x 0 0 0 1 x x x 0 0 0 0 x x x 0 0 0 1 x x x 0 0 0 0 x x x 0 0 0 1 x x x 0 0 0 0 x x x 0 0 0 1 x x x 0 0 0 0 x x x 0 0 0 1 x x x 0 0 0 0 x x x 0 0 0 1 x x x 0 0 0 0 x x x 0 0 0 1 x x x 0 0 0 0 x x x 0 0 0 1 x x x 0 0 0 0 x x x 0 0 0 1 x x x 0 0 0 0 x x x 0 0 0 1 x x x 0 0 0 0 x x x 0 0 0 1 x x x 0 0 0 0 x x x 0 0 0 1 x x x 0 0 0 0 x x x 0 0 0 1 x x x 0 0 0 0 x x x 0 0 0 1 x x x 0 0 0 0 x x x 0 0 0 1 x x x 0 0 0 0 x x x 0 0 0 1 x x x 0 0 0 0 2 27 0 0 0 0 1 2 27 0 30 1 0 0 x x x 30 1 0 1 x x 1 0 0 0 0 x x x 0 0 0 1 x x x 0 0 0 0 x x x 0 0 0 1 x x x 0 0 0 0 x x x 0 0 0 1 x x x 0 0 0 0 x x x 0 0 0 1 x x x 0 0 0 0 x x x 0 0 0 1 x x x 0 0 0 0 x x x 0 0 0 1 x x x 0 0 0 0 x x x 0 0 0 1 x x x 0 0 0 0 x x x 0 0 0 1 x x x 0 0 0 0 x x x 0 0 0 1 x x x 0 0 0 0 x x x 0 0 0 1 x x x 0 0 0 0 x x x 0 0 0 1 x x x 0 0 0 0 x x x 0 0 0 1 x x x 0 0 0 0 x x x 0 0 0 1 x x x 0 0 0 0 x x x 0 0 0 1 x x x 0 0 0 0 x x x 0 0 0 1 x x x 0 0 0 0 x x x 0 0 0 1 x x x 0 0 0 0 x x x 0 0 0 1 x x x 0 0 0 0 x x x 0 0 0 1 x x x 0 0 0 0 x x x 0 0 0 1 x x x 0 0 0 0 x x x 0 0 0 1 x x x 0 0 0 0 x x x 0 0 0 1 x x x 0 0 0 0 x x x 0 0 0 1 x x x 0 0 0 0 x x x 0 0 0 1 x x x 0 0 0 0 x x x 0 0 0 1 x x x 0 0 0 0 x x x 0 0 0 1 x x x 0 0 0 0 x x x 0 0 0 1 x x x 0 0 0 0 x x x 0 0 0 1 x x x 0 0 0 0 x x x 0 0 0 1 x x x 0 0 0 0 x x x 0 0 0 1 x x x 0 0 0 0 x x x 0 0 0 1 x x x 0 0 0 0 3 30 0 0 0 0 1 3 30 0 21 1 0 0 x x x 21 1 0 1 x x 1 0 0 0 0 x x x 0 0 0 1 x x x 0 0 0 0 x x x 0 0 0 1 x x x 0 0 0 0 x x x 0 0 0 1 x x x 0 0 0 0 x x x 0 0 0 1 x x x 0 0 0 0 x x x 0 0 0 1 x x x 0 0 0 0 x x x 0 0 0 1 x x x 0 0 0 0 x x x 0 0 0 1 x x x 0 0 0 0 x x x 0 0 0 1 x x x 0 0 0 0 x x x 0 0 0 1 x x x 0 0 0 0 x x x 0 0 0 1 x x x 0 0 0 0 x x x 0 0 0 1 x x x
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*/

/* Test case T01:
N new reset clock num_inc max busy 0 0 1 0 x x x 0 0 1 1 0 0 0 1 1 0 0 x x x 1 1 0 1 x x 1 0 0 0 0 x x x 0 0 0 1 x x x 0 0 0 0 x x x 0 0 0 1 x x x 0 0 0 0 x x x 0 0 0 1 x x x 0 0 0 0 x x x 0 0 0 1 x x x 0 0 0 0 x x x 0 0 0 1 x x x 0 0 0 0 x x x 0 0 0 1 x x x 0 0 0 0 x x x 0 0 0 1 x x x 0 0 0 0 x x x 0 0 0 1 x x x 0 0 0 0 x x x 0 0 0 1 x x x 0 0 0 0 x x x 0 0 0 1 x x x 0 0 0 0 x x x 0 0 0 1 x x x 0 0 0 0 x x x 0 0 0 1 x x x 0 0 0 0 x x x 0 0 0 1 x x x 0 0 0 0 x x x 0 0 0 1 x x x 0 0 0 0 x x x 0 0 0 1 x x x 0 0 0 0 x x x 0 0 0 1 x x x 0 0 0 0 x x x 0 0 0 1 x x x 0 0 0 0 x x x 0 0 0 1 x x x 0 0 0 0 x x x 0 0 0 1 x x x 0 0 0 0 x x x 0 0 0 1 x x x 0 0 0 0 x x x 0 0 0 1 x x x 0 0 0 0 x x x 0 0 0 1 x x x 0 0 0 0 x x x 0 0 0 1 x x x 0 0 0 0 x x x 0 0 0 1 x x x 0 0 0 0 x x x 0 0 0 1 x x x 0 0 0 0 x x x 0 0 0 1 x x x 0 0 0 0 x x x 0 0 0 1 x x x 0 0 0 0 x x x 0 0 0 1 x x x 0 0 0 0 x x x 0 0 0 1 x x x 0 0 0 0 x x x 0 0 0 1 x x x 0 0 0 0 1 1 0 0 0 0 1 1 1 0 1 1 0 0 x x x 1 1 0 1 x x 1 0 0 0 0 x x x 0 0 0 1 x x x 0 0 0 0 x x x 0 0 0 1 x x x 0 0 0 0 x x x 0 0 0 1 x x x 0 0 0 0 x x x 0 0 0 1 x x x 0 0 0 0 x x x 0 0 0 1 x x x 0 0 0 0 x x x 0 0 0 1 x x x 0 0 0 0 x x x 0 0 0 1 x x x 0 0 0 0 x x x 0 0 0 1 x x x 0 0 0 0 x x x 0 0 0 1 x x x 0 0 0 0 x x x 0 0 0 1 x x x 0 0 0 0 x x x 0 0 0 1 x x x 0 0 0 0 x x x 0 0 0 1 x x x 0 0 0 0 x x x 0 0 0 1 x x x 0 0 0 0 x x x 0 0 0 1 x x x 0 0 0 0 x x x 0 0 0 1 x x x 0 0 0 0 x x x 0 0 0 1 x x x 0 0 0 0 x x x 0 0 0 1 x x x 0 0 0 0 x x x 0 0 0 1 x x x 0 0 0 0 x x x 0 0 0 1 x x x 0 0 0 0 x x x 0 0 0 1 x x x 0 0 0 0 x x x 0 0 0 1 x x x 0 0 0 0 x x x 0 0 0 1 x x x 0 0 0 0 x x x 0 0 0 1 x x x 0 0 0 0 x x x 0 0 0 1 x x x 0 0 0 0 x x x 0 0 0 1 x x x 0 0 0 0 x x x 0 0 0 1 x x x 0 0 0 0 x x x 0 0 0 1 x x x 0 0 0 0 x x x 0 0 0 1 x x x 0 0 0 0 x x x 0 0 0 1 x x x 0 0 0 0 x x x 0 0 0 1 x x x 0 0 0 0 1 1 0 0 0 0 1 1 1 0 1 1 0 0 x x x 1 1 0 1 x x 1 0 0 0 0 x x x 0 0 0 1 x x x 0 0 0 0 x x x 0 0 0 1 x x x 0 0 0 0 x x x 0 0 0 1 x x x 0 0 0 0 x x x 0 0 0 1 x x x 0 0 0 0 x x x 0 0 0 1 x x x 0 0 0 0 x x x 0 0 0 1 x x x 0 0 0 0 x x x 0 0 0 1 x x x 0 0 0 0 x x x 0 0 0 1 x x x 0 0 0 0 x x x 0 0 0 1 x x x 0 0 0 0 x x x 0 0 0 1 x x x 0 0 0 0 x x x 0 0 0 1 x x x 0 0 0 0 x x x 0 0 0 1 x x x 0 0 0 0 x x x 0 0 0 1 x x x 0 0 0 0 x x x 0 0 0 1 x x x 0 0 0 0 x x x 0 0 0 1 x x x 0 0 0 0 x x x 0 0 0 1 x x x 0 0 0 0 x x x 0 0 0 1 x x x 0 0 0 0 x x x 0 0 0 1 x x x 0 0 0 0 x x x 0 0 0 1 x x x 0 0 0 0 x x x 0 0 0 1 x x x 0 0 0 0 x x x 0 0 0 1 x x x 0 0 0 0 x x x 0 0 0 1 x x x 0 0 0 0 x x x 0 0 0 1 x x x 0 0 0 0 x x x 0 0 0 1 x x x 0 0 0 0 x x x 0 0 0 1 x x x 0 0 0 0 x x x 0 0 0 1 x x x 0 0 0 0 x x x 0 0 0 1 x x x 0 0 0 0 x x x 0 0 0 1 x x x 0 0 0 0 x x x 0 0 0 1 x x x 0 0 0 0 x x x 0 0 0 1 x x x 0 0 0 0 1 1 0 0 0 0 1 1 1 0 1 1 0 0 x x x 1 1 0 1 x x 1 0 0 0 0 x x x 0 0 0 1 x x x 0 0 0 0 x x x 0 0 0 1 x x x 0 0 0 0 x x x 0 0 0 1 x x x 0 0 0 0 x x x 0 0 0 1 x x x 0 0 0 0 x x x 0 0 0 1 x x x 0 0 0 0 x x x 0 0 0 1 x x x 0 0 0 0 x x x 0 0 0 1 x x x 0 0 0 0 x x x 0 0 0 1 x x x 0 0 0 0 x x x 0 0 0 1 x x x 0 0 0 0 x x x 0 0 0 1 x x x 0 0 0 0 x x x 0 0 0 1 x x x 0 0 0 0 x x x 0 0 0 1 x x x 0 0 0 0 x x x 0 0 0 1 x x x 0 0 0 0 x x x 0 0 0 1 x x x 0 0 0 0 x x x 0 0 0 1 x x x 0 0 0 0 x x x 0 0 0 1 x x x 0 0 0 0 x x x 0 0 0 1 x x x 0 0 0 0 x x x 0 0 0 1 x x x 0 0 0 0 x x x 0 0 0 1 x x x 0 0 0 0 x x x 0 0 0 1 x x x 0 0 0 0 x x x 0 0 0 1 x x x 0 0 0 0 x x x 0 0 0 1 x x x 0 0 0 0 x x x 0 0 0 1 x x x 0 0 0 0 x x x 0 0 0 1 x x x 0 0 0 0 x x x 0 0 0 1 x x x 0 0 0 0 x x x 0 0 0 1 x x x 0 0 0 0 x x x 0 0 0 1 x x x 0 0 0 0 x x x 0 0 0 1 x x x 0 0 0 0 x x x 0 0 0 1 x x x 0 0 0 0 x x x 0 0 0 1 x x x 0 0 0 0 1 1 0 0 0 0 1 1 1 0 1 1 0 0 x x x 1 1 0 1 x x 1 0 0 0 0 x x x 0 0 0 1 x x x 0 0 0 0 x x x 0 0 0 1 x x x 0 0 0 0 x x x 0 0 0 1 x x x 0 0 0 0 x x x 0 0 0 1 x x x 0 0 0 0 x x x 0 0 0 1 x x x 0 0 0 0 x x x 0 0 0 1 x x x 0 0 0 0 x x x 0 0 0 1 x x x 0 0
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*/
